// Logisim project Branch.circ as structural Verilog: 2 circuits, main circuit Branch
module Branch (
  input  [3:0] branchop,
  input  ALUzero,
  input  ALUnega,
  output isBranch
);

  wire bge, bgt, ble, blt, bne;

  not not_1 (bne, ALUzero);
  and and_1 (bgt, ~ALUzero, ~ALUnega);  // AND_Gate
  and and_2 (blt, ~ALUzero, ALUnega);  // AND_Gate
  not not_2 (bge, ALUnega);
  or or_1 (ble, ALUzero, ALUnega);
  Pull_Resistor pull_resistor_1 (.node(isBranch));
  Multiplexer #(.select(4), .disabled(0), .enable("false")) multiplexer_1 (
    .in0(1'b0), .in1(ALUzero), .in2(bne), .in3(bgt), .in4(blt), .in5(bge), .in6(ble), .out(isBranch),
    .sel(branchop));  // open: in7, in8, in9, in10, in11, in12, in13, in14, in15

  // Other names for the same wires on the sheet: nega = ALUnega; beq = ALUzero; zero = ALUzero

  // Notes on the sheet:
  //   分支控制器：令ALU做减法，以其输出的标志信号来判断大小关系从而确定跳转
  //   0001:相等, 0010:不等, 0011:大于，0100:小于
  //   0101:大于等于，0110:小于等于
endmodule

module test (
  input  in_1,
  input  [3:0] in_2,
  input  in_3,
  output out_4
);

  Branch branch_1 (.branchop(in_2), .ALUzero(in_1), .ALUnega(in_3), .isBranch(out_4));
endmodule
