// Logisim project CPU.circ as structural Verilog: 24 circuits, main circuit main
module main (
  input  rst,
  output [31:0] Instr,
  output RegWrite,
  output [4:0] RegAddr,
  output [31:0] RegData,
  output MemWrite,
  output [4:0] MemAddr,
  output [31:0] MemData
);

  wire ALUsrc, and_1_out, and_2_out, and_3_out, Branch, BRspc, CALCsrc, clock_1_out, clock_2_out,
       clock_3_out, comp_1_out, Dext, EXTop, JmpLnk, JmpSrc, Jump, MemtoReg, negaflg, SHsrc, zeroflg;
  wire [1:0] Dsize, RegDst;
  wire [2:0] NPCop, SHop;
  wire [3:0] ALUop, BRop;
  wire [4:0] bit_extender_1_out, GRF_A1, GRF_A2, multiplexer_6_out, rd, rt, shamt;
  wire [5:0] funct, op;
  wire [15:0] imm;
  wire [25:0] addr;
  wire [31:0] ALUresult, ALUsrcA, ALUsrcB, CALCresult, DM_RD, DM_WD, ExtImm, multiplexer_3_out, nextPC, PC,
       PC_4, SHIFTresult;

  PC pc_1 (.nextPC(nextPC), .PC(PC), .clk(clock_1_out), .rst(rst));
  Clock clock_1 (.out(clock_1_out));
  COMP comp_1 (.A(ALUsrcA), .B(DM_WD), .CMPop(BRop), .out(comp_1_out));
  NPC npc_1 (.PC(PC), .imm16(imm), .addr26(addr), .ra32(ALUsrcA), .op(NPCop), .nextPC(nextPC), .PC4(PC_4));
  IM im_1 (.A(PC), .RD(Instr));
  and and_1 (and_1_out, Branch, comp_1_out);
  and and_2 (and_2_out, Jump, ~JmpSrc);  // AND_Gate
  and and_3 (and_3_out, Jump, JmpSrc);
  Priority_Encoder priority_encoder_1 (
    .in0(1'b1), .in1(and_1_out), .in2(and_2_out), .in3(and_3_out), .out(NPCop));  // open: in4, in5, in6, in7, en_in, gs, en_out
  Control control_1 (
    .opcode(op), .funct(funct), .MemtoReg(MemtoReg), .MemWrite(MemWrite), .ALUop(ALUop), .EXTop(EXTop),
    .ALUsrc(ALUsrc), .RegDst(RegDst), .RegWrite(RegWrite), .BRop(BRop), .Jump(Jump), .JmpSrc(JmpSrc),
    .JmpLnk(JmpLnk), .Branch(Branch), .Dsize(Dsize), .Dext(Dext), .rs(GRF_A1), .rt(rt), .CALCsrc(CALCsrc),
    .SHop(SHop), .SHsrc(SHsrc), .BRspc(BRspc));
  ISplitter isplitter_1 (
    .Instr(Instr), .op(op), .rs(GRF_A1), .rt(rt), .rd(rd), .shamt(shamt), .funct(funct), .imm(imm),
    .addr(addr));
  Multiplexer #(.select(2), .width(5), .disabled(0), .enable("false")) multiplexer_1 (
    .in0(rd), .in1(rt), .in2({5{1'b1}}), .out(RegAddr), .sel(RegDst));  // open: in3
  Multiplexer #(.width(5), .disabled(0), .enable("false")) multiplexer_2 (
    .in0(rt), .in1({5{1'b0}}), .out(GRF_A2), .sel(BRspc));
  GRF grf_1 (
    .A1(GRF_A1), .A2(GRF_A2), .A3(RegAddr), .WD(RegData), .RD1(ALUsrcA), .RD2(DM_WD), .clk(clock_2_out),
    .reset(rst), .WE(RegWrite));
  Clock clock_2 (.out(clock_2_out));
  EXT ext_1 (.in(imm), .EXTop(EXTop), .out(ExtImm));
  Multiplexer #(.width(32), .disabled(0), .enable("false")) multiplexer_3 (
    .in0(CALCresult), .in1(DM_RD), .out(multiplexer_3_out), .sel(MemtoReg));
  Multiplexer #(.width(32), .disabled(0), .enable("false")) multiplexer_4 (
    .in0(multiplexer_3_out), .in1(PC_4), .out(RegData), .sel(JmpLnk));
  Multiplexer #(.width(32), .disabled(0), .enable("false")) multiplexer_5 (
    .in0(DM_WD), .in1(ExtImm), .out(ALUsrcB), .sel(ALUsrc));
  ALU alu_1 (.A(ALUsrcA), .B(ALUsrcB), .Op(ALUop), .Out(ALUresult), .zero(zeroflg), .nega(negaflg));
  Bit_Extender #(.in_width(32), .out_width(5)) bit_extender_1 (.in(ALUsrcA), .out(bit_extender_1_out));
  Multiplexer #(.width(5), .enable("false")) multiplexer_6 (
    .in0(shamt), .in1(bit_extender_1_out), .out(multiplexer_6_out), .sel(SHsrc));
  Shifter shifter_1 (.In(DM_WD), .sh(multiplexer_6_out), .op(SHop), .Out(SHIFTresult));
  Multiplexer #(.width(32), .disabled(0), .enable("false")) multiplexer_7 (
    .in0(ALUresult), .in1(SHIFTresult), .out(CALCresult), .sel(CALCsrc));
  DM dm_1 (
    .A(CALCresult), .WD(DM_WD), .RD(DM_RD), .clk(clock_3_out), .rst(rst), .WE(MemWrite), .extop(Dext),
    .size(Dsize), .WT(MemData), .WAddr5(MemAddr));
  Clock clock_3 (.out(clock_3_out));

  // Other names for the same wires on the sheet: DM_A[31:0] = CALCresult; GRF_A3[4:0] = RegAddr;
  //   GRF_RD1[31:0] = ALUsrcA; GRF_RD2[31:0] = DM_WD; GRF_WD[31:0] = RegData; rs[4:0] = GRF_A1

  // Notes on the sheet:
  //   取指令IF阶段
  //   这个信号其实应该在EX阶段
  //   译码ID阶段
  //   寄存器回写WB阶段
  //   执行EX阶段
  //   访存MEM阶段
endmodule

module GlobalConstant (
  output \config 
);


  assign \config  = 1'b0;

  // Notes on the sheet:
  //   Global Constant 模块：全局常量
  //   用途：根据参数调整电路，以便应对本地和计组平台上的不同规格要求
  //   1表示按照cscore平台，0表示本地自己用
endmodule

module PC (
  input  clk,
  input  rst,
  input  [31:0] nextPC,
  output [31:0] PC
);

  wire comparator_1_lt, globalconstant_1_config, init;
  wire [31:0] multiplexer_1_out, multiplexer_2_out, PC_q, subtractor_1_out;

  Counter #(.width(1), .max('h1), .ongoal("stay")) initcnt (
    .carry(init), .clk(clk), .clr(rst));  // open: load, D, count, Q
  GlobalConstant globalconstant_1 (.\config (globalconstant_1_config));
  Register #(.width(32)) u_PC (.D(nextPC), .Q(PC_q), .clk(clk), .clr(rst));  // open: en
  Multiplexer #(.width(32), .disabled(0), .enable("false")) multiplexer_1 (
    .in0(32'h3000), .in1({32{1'b0}}), .out(multiplexer_1_out), .sel(globalconstant_1_config));
  Multiplexer #(.width(32), .disabled(0), .enable("false")) multiplexer_2 (
    .in0(multiplexer_1_out), .in1(PC_q), .out(multiplexer_2_out), .sel(init));
  // Probe on multiplexer_2_out
  Subtractor #(.width(32)) subtractor_1 (
    .a(multiplexer_2_out), .b(32'h3000), .out(subtractor_1_out));  // open: bin, bout
  Comparator #(.width(32), .mode("unsigned")) comparator_1 (
    .a(multiplexer_2_out), .b(32'h3000), .lt(comparator_1_lt));  // open: gt, eq
  Multiplexer #(.width(32), .disabled(0), .enable("false")) multiplexer_3 (
    .in0(subtractor_1_out), .in1(multiplexer_2_out), .out(PC), .sel(comparator_1_lt));

  // Notes on the sheet:
  //   Program Counter: 指令计数器
  //   不管你在强测中得了多少分......
  //   select for J
endmodule

module NPC (
  input  [31:0] PC,
  input  [15:0] imm16,
  input  [25:0] addr26,
  input  [31:0] ra32,
  input  [2:0] op,
  output [31:0] nextPC,
  output [31:0] PC4
);

  wire [31:0] bit_extender_1_out, branch, imm;

  assign bit_extender_1_out = {{16{imm16[15]}}, imm16};  // Bit_Extender bit_extender_1
  Shifter_part #(.width(32)) shifter_1 (.in(bit_extender_1_out), .\dist (5'b00010), .out(imm));
  Adder #(.width(32)) adder_1 (.a(PC), .b(32'h4), .out(PC4));  // open: cin, cout
  Adder #(.width(32)) adder_2 (.a(PC4), .b(imm), .out(branch));  // open: cin, cout
  Multiplexer #(.select(3), .width(32), .disabled(0), .enable("false")) multiplexer_1 (
    .in0(PC4), .in1(branch), .in2({PC4[31:28], addr26, 2'b00}), .in3(ra32), .out(nextPC), .sel(op));  // open: in4, in5, in6, in7

  // Other names for the same wires on the sheet: addr[31:2] = {PC4[31:28], addr26}; ra[31:0] = ra32

  // Notes on the sheet:
  //   NPC模块:Next PC，计算下一路PC的值
endmodule

module IM (
  input  [31:0] A,
  output [31:0] RD
);

  wire [4:0] im_addr5_1_addr5;

  // Probe on A
  im_addr5 im_addr5_1 (.Addr32(A), .Addr5(im_addr5_1_addr5));
  ROM #(.addrWidth(5), .dataWidth(32)) rom_1 (.addr(im_addr5_1_addr5), .data(RD), .sel(1'b1));
  // Probe on RD

  // Notes on the sheet:
  //   Instruction Memory 指令存储器
  //   im_addr模块将32位的PC转化成5位的ROM地址
  //   contents of rom_1 (hex, n*v repeats v):
  //   341c0000 341d0000 340080f8 36ee0367 3593769c 34dda539 3465c5dc 34be0ff1 3472af1d 35566602 35fe72a7
  //   3437ff23 37b9649e 3690bf9b 37fe4e0c 3711f49d 3c113bfe 3c057433 3c03c451 3c04c431 3c1c24d9 3c1bf0da
  //   3c0ccc68 3c0a118d 3c1021ea 3c0004d3 3c16115b 3c184f06 3c1215de 1000ffff
endmodule

module im_addr24 (
  input  [31:0] Addr32,
  output [23:0] Addr24
);

  wire [31:0] shifter_1_out, subtractor_1_out;

  Subtractor #(.width(32)) subtractor_1 (.a(Addr32), .b(32'h3000), .out(subtractor_1_out));  // open: bin, bout
  Shifter_part #(.width(32), .shift("lr")) shifter_1 (.in(subtractor_1_out), .\dist (5'b00010), .out(shifter_1_out));
  Bit_Extender #(.in_width(32), .out_width(24)) bit_extender_1 (.in(shifter_1_out), .out(Addr24));

  // Notes on the sheet:
  //   im_addr: 将32位的地址转化为24位的适合ROM的地址
  //   注：若PC地址从0x00003000开始
endmodule

module im_addr5 (
  input  [31:0] Addr32,
  output [4:0] Addr5
);

  wire [31:0] shifter_1_out;

  Shifter_part #(.width(32), .shift("lr")) shifter_1 (.in(Addr32), .\dist (5'b00010), .out(shifter_1_out));
  Bit_Extender #(.in_width(32), .out_width(5)) bit_extender_1 (.in(shifter_1_out), .out(Addr5));

  // Notes on the sheet:
  //   im_addr5: 将32位的地址转化为5位的适合ROM的地址
endmodule

module ISplitter (
  input  [31:0] Instr,
  output [5:0] op,
  output [4:0] rs,
  output [4:0] rt,
  output [4:0] rd,
  output [4:0] shamt,
  output [5:0] funct,
  output [15:0] imm,
  output [25:0] addr
);


  assign addr = Instr[25:0];
  assign funct = Instr[5:0];
  assign imm = Instr[15:0];
  assign op = Instr[31:26];
  assign rd = Instr[15:11];
  assign rs = Instr[25:21];
  assign rt = Instr[20:16];
  assign shamt = Instr[10:6];

  // Notes on the sheet:
  //   Instruction Splitter(ISplitter)模块：将指令的每个部分拆分出来
  //   将32位的指令按照R,I,J型指令将每个部分拆分出来
  //   R-type
  //   I-type
  //   J-type
endmodule

module GRF (
  input  clk,
  input  reset,
  input  WE,
  input  [4:0] A1,
  input  [4:0] A2,
  input  [4:0] A3,
  input  [31:0] WD,
  output [31:0] RD1,
  output [31:0] RD2
);

  wire E1, E2, E3, E4, E5, E6, E7, E8, E9, E10, E11, E12, E13, E14, E15, E16, E17, E18, E19, E20, E21, E22,
       E23, E24, E25, E26, E27, E28, E29, E30, E31;
  wire [31:0] D1, D2, D3, D4, D5, D6, D7, D8, D9, D10, D11, D12, D13, D14, D15, D16, D17, D18, D19, D20, D21,
       D22, D23, D24, D25, D26, D27, D28, D29, D30, D31, Q0, Q1, Q2, Q3, Q4, Q5, Q6, Q7, Q8, Q9, Q10, Q11,
       Q12, Q13, Q14, Q15, Q16, Q17, Q18, Q19, Q20, Q21, Q22, Q23, Q24, Q25, Q26, Q27, Q28, Q29, Q30, Q31;

  Demultiplexer #(.select(5), .disabled(0), .enable("false")) demultiplexer_1 (
    .out1(E1), .out2(E2), .out3(E3), .out4(E4), .out5(E5), .out6(E6), .out7(E7), .out8(E8), .out9(E9),
    .out10(E10), .out11(E11), .out12(E12), .out13(E13), .out14(E14), .out15(E15), .out16(E16), .out17(E17),
    .out18(E18), .out19(E19), .out20(E20), .out21(E21), .out22(E22), .out23(E23), .out24(E24), .out25(E25),
    .out26(E26), .out27(E27), .out28(E28), .out29(E29), .out30(E30), .out31(E31), .in(WE), .sel(A3));  // open: out0
  Register #(.width(32)) reg0 (.en(1'b0), .Q(Q0), .clk(clk), .clr(reset));  // open: D
  Register #(.width(32)) reg8 (.D(D8), .en(E8), .Q(Q8), .clk(clk), .clr(reset));
  Register #(.width(32)) reg16 (.D(D16), .en(E16), .Q(Q16), .clk(clk), .clr(reset));
  Register #(.width(32)) reg24 (.D(D24), .en(E24), .Q(Q24), .clk(clk), .clr(reset));
  Register #(.width(32)) reg1 (.D(D1), .en(E1), .Q(Q1), .clk(clk), .clr(reset));
  Register #(.width(32)) reg9 (.D(D9), .en(E9), .Q(Q9), .clk(clk), .clr(reset));
  Register #(.width(32)) reg17 (.D(D17), .en(E17), .Q(Q17), .clk(clk), .clr(reset));
  Register #(.width(32)) reg25 (.D(D25), .en(E25), .Q(Q25), .clk(clk), .clr(reset));
  Demultiplexer #(.select(5), .width(32), .disabled(0), .enable("false")) demultiplexer_2 (
    .out1(D1), .out2(D2), .out3(D3), .out4(D4), .out5(D5), .out6(D6), .out7(D7), .out8(D8), .out9(D9),
    .out10(D10), .out11(D11), .out12(D12), .out13(D13), .out14(D14), .out15(D15), .out16(D16), .out17(D17),
    .out18(D18), .out19(D19), .out20(D20), .out21(D21), .out22(D22), .out23(D23), .out24(D24), .out25(D25),
    .out26(D26), .out27(D27), .out28(D28), .out29(D29), .out30(D30), .out31(D31), .in(WD), .sel(A3));  // open: out0
  Register #(.width(32)) reg2 (.D(D2), .en(E2), .Q(Q2), .clk(clk), .clr(reset));
  Register #(.width(32)) reg10 (.D(D10), .en(E10), .Q(Q10), .clk(clk), .clr(reset));
  Register #(.width(32)) reg18 (.D(D18), .en(E18), .Q(Q18), .clk(clk), .clr(reset));
  Register #(.width(32)) reg26 (.D(D26), .en(E26), .Q(Q26), .clk(clk), .clr(reset));
  Register #(.width(32)) reg3 (.D(D3), .en(E3), .Q(Q3), .clk(clk), .clr(reset));
  Register #(.width(32)) reg11 (.D(D11), .en(E11), .Q(Q11), .clk(clk), .clr(reset));
  Register #(.width(32)) reg19 (.D(D19), .en(E19), .Q(Q19), .clk(clk), .clr(reset));
  Register #(.width(32)) reg27 (.D(D27), .en(E27), .Q(Q27), .clk(clk), .clr(reset));
  Register #(.width(32)) reg4 (.D(D4), .en(E4), .Q(Q4), .clk(clk), .clr(reset));
  Register #(.width(32)) reg12 (.D(D12), .en(E12), .Q(Q12), .clk(clk), .clr(reset));
  Register #(.width(32)) reg20 (.D(D20), .en(E20), .Q(Q20), .clk(clk), .clr(reset));
  Register #(.width(32)) reg28 (.D(D28), .en(E28), .Q(Q28), .clk(clk), .clr(reset));
  Multiplexer #(.select(5), .width(32), .disabled(0), .enable("false")) multiplexer_1 (
    .in0(Q0), .in1(Q1), .in2(Q2), .in3(Q3), .in4(Q4), .in5(Q5), .in6(Q6), .in7(Q7), .in8(Q8), .in9(Q9),
    .in10(Q10), .in11(Q11), .in12(Q12), .in13(Q13), .in14(Q14), .in15(Q15), .in16(Q16), .in17(Q17),
    .in18(Q18), .in19(Q19), .in20(Q20), .in21(Q21), .in22(Q22), .in23(Q23), .in24(Q24), .in25(Q25),
    .in26(Q26), .in27(Q27), .in28(Q28), .in29(Q29), .in30(Q30), .in31(Q31), .out(RD1), .sel(A1));
  Register #(.width(32)) reg5 (.D(D5), .en(E5), .Q(Q5), .clk(clk), .clr(reset));
  Register #(.width(32)) reg13 (.D(D13), .en(E13), .Q(Q13), .clk(clk), .clr(reset));
  Register #(.width(32)) reg21 (.D(D21), .en(E21), .Q(Q21), .clk(clk), .clr(reset));
  Register #(.width(32)) reg29 (.D(D29), .en(E29), .Q(Q29), .clk(clk), .clr(reset));
  Register #(.width(32)) reg6 (.D(D6), .en(E6), .Q(Q6), .clk(clk), .clr(reset));
  Register #(.width(32)) reg14 (.D(D14), .en(E14), .Q(Q14), .clk(clk), .clr(reset));
  Register #(.width(32)) reg22 (.D(D22), .en(E22), .Q(Q22), .clk(clk), .clr(reset));
  Register #(.width(32)) reg30 (.D(D30), .en(E30), .Q(Q30), .clk(clk), .clr(reset));
  Multiplexer #(.select(5), .width(32), .disabled(0), .enable("false")) multiplexer_2 (
    .in0(Q0), .in1(Q1), .in2(Q2), .in3(Q3), .in4(Q4), .in5(Q5), .in6(Q6), .in7(Q7), .in8(Q8), .in9(Q9),
    .in10(Q10), .in11(Q11), .in12(Q12), .in13(Q13), .in14(Q14), .in15(Q15), .in16(Q16), .in17(Q17),
    .in18(Q18), .in19(Q19), .in20(Q20), .in21(Q21), .in22(Q22), .in23(Q23), .in24(Q24), .in25(Q25),
    .in26(Q26), .in27(Q27), .in28(Q28), .in29(Q29), .in30(Q30), .in31(Q31), .out(RD2), .sel(A2));
  Register #(.width(32)) reg7 (.D(D7), .en(E7), .Q(Q7), .clk(clk), .clr(reset));
  Register #(.width(32)) reg15 (.D(D15), .en(E15), .Q(Q15), .clk(clk), .clr(reset));
  Register #(.width(32)) reg23 (.D(D23), .en(E23), .Q(Q23), .clk(clk), .clr(reset));
  Register #(.width(32)) reg31 (.D(D31), .en(E31), .Q(Q31), .clk(clk), .clr(reset));
endmodule

module COMP (
  input  [31:0] A,
  input  [31:0] B,
  input  [3:0] CMPop,
  output out
);

  wire comparator_1_eq, comparator_1_gt, comparator_1_lt, not_1_out, not_2_out, not_3_out, undriven;

  Pull_Resistor pull_resistor_1 (.node(A));
  Pull_Resistor pull_resistor_2 (.node(B));
  Comparator #(.width(32)) comparator_1 (
    .a(A), .b(B), .gt(comparator_1_gt), .eq(comparator_1_eq), .lt(comparator_1_lt));
  not not_1 (not_1_out, comparator_1_eq);
  not not_2 (not_2_out, comparator_1_lt);
  not not_3 (not_3_out, comparator_1_gt);
  Pull_Resistor pull_resistor_3 (.node(out));
  Multiplexer #(.select(4), .disabled(0), .enable("false")) multiplexer_1 (
    .in0(comparator_1_eq), .in1(not_1_out), .in2(not_2_out), .in3(comparator_1_gt), .in4(not_3_out),
    .in5(comparator_1_lt), .in6(undriven), .out(out), .sel(CMPop));  // open: in7, in8, in9, in10, in11, in12, in13, in14, in15

  // Notes on the sheet:
  //   分支比较器模块
  //   输出：按照指定比较条件，结果是否为真
  //   000: eq, 001: ne, 010: ge, 011: gt, 100: le, 101: lt
endmodule

module EXT (
  input  [15:0] in,
  input  EXTop,
  output [31:0] out
);

  wire [31:0] bit_extender_1_out, bit_extender_2_out;

  assign bit_extender_1_out = {{16{1'b0}}, in};  // Bit_Extender bit_extender_1
  assign bit_extender_2_out = {{16{in[15]}}, in};  // Bit_Extender bit_extender_2
  Multiplexer #(.width(32), .disabled(0), .enable("false")) multiplexer_1 (
    .in0(bit_extender_1_out), .in1(bit_extender_2_out), .out(out), .sel(EXTop));
endmodule

module ALU (
  input  [31:0] A,
  input  [31:0] B,
  input  [3:0] Op,
  output [31:0] Out,
  output zero,
  output nega
);

  wire comparator_1_lt, comparator_2_lt;
  wire [31:0] add, \and , lui, \nor , \or , slt, sltu, sub, \xor ;

  Adder #(.width(32)) adder_1 (.a(A), .b(B), .out(add));  // open: cin, cout
  Subtractor #(.width(32)) subtractor_1 (.a(A), .b(B), .out(sub));  // open: bin, bout
  assign \and  = A & B;  // AND_Gate and_1, 32 bits wide
  assign \or  = A | B;  // OR_Gate or_1, 32 bits wide
  assign \nor  = ~(A | B);  // NOR_Gate nor_1, 32 bits wide
  assign \xor  = A ^ B;  // XOR_Gate xor_1, 32 bits wide
  Comparator #(.width(32)) comparator_1 (.a(A), .b(B), .lt(comparator_1_lt));  // open: gt, eq
  Shifter_part #(.width(32)) shifter_1 (.in(B), .\dist (5'b10000), .out(lui));
  Comparator #(.width(32), .mode("unsigned")) comparator_2 (.a(A), .b(B), .lt(comparator_2_lt));  // open: gt, eq
  assign slt = {{31{1'b0}}, comparator_1_lt};  // Bit_Extender bit_extender_1
  assign sltu = {{31{1'b0}}, comparator_2_lt};  // Bit_Extender bit_extender_2
  Multiplexer #(.select(4), .width(32), .disabled(0), .enable("false")) multiplexer_1 (
    .in0(add), .in1(sub), .in2(\and ), .in3(\or ), .in4(\nor ), .in5(\xor ), .in6(slt), .in7(sltu),
    .in8(lui), .out(Out), .sel(Op));  // open: in9, in10, in11, in12, in13, in14, in15
  Pull_Resistor pull_resistor_1 (.node(Out));
  Comparator #(.width(32)) comparator_3 (.a(Out), .b({32{1'b0}}), .eq(zero), .lt(nega));  // open: gt

  // Notes on the sheet:
  //   ALU 算术逻辑单元
endmodule

module Shifter (
  input  [31:0] In,
  input  [4:0] sh,
  input  [2:0] op,
  output [31:0] Out
);

  wire [31:0] aright, lleft, lright, rleft, rright;

  Shifter_part #(.width(32)) shifter_1 (.in(In), .\dist (sh), .out(lleft));
  Shifter_part #(.width(32), .shift("lr")) shifter_2 (.in(In), .\dist (sh), .out(lright));
  Shifter_part #(.width(32), .shift("ar")) shifter_3 (.in(In), .\dist (sh), .out(aright));
  Shifter_part #(.width(32), .shift("rl")) shifter_4 (.in(In), .\dist (sh), .out(rleft));
  Shifter_part #(.width(32), .shift("rr")) shifter_5 (.in(In), .\dist (sh), .out(rright));
  Multiplexer #(.select(3), .width(32), .disabled(0), .enable("false")) multiplexer_1 (
    .in0(lleft), .in1(lright), .in2(aright), .in3(rleft), .in4(rright), .out(Out), .sel(op));  // open: in5, in6, in7
  Pull_Resistor pull_resistor_1 (.node(Out));

  // Notes on the sheet:
  //   移位器：In 32位输入，sh 5位输入-移位的数目，op 3位 操作种类
  //   op对应的操作种类： 000:左移，001:逻辑右移，010:算术右移，011:循环左移，100: 循环右移
endmodule

module DM (
  input  clk,
  input  rst,
  input  WE,
  input  [1:0] size,
  input  extop,
  input  [31:0] A,
  input  [31:0] WD,
  output [31:0] RD,
  output [31:0] WT,
  output [4:0] WAddr5
);

  wire decoder_1_out0, decoder_1_out1, decoder_1_out2, decoder_1_out3, decoder_2_out0, decoder_2_out1,
       offset_half;
  wire [1:0] offset_byte;
  wire [7:0] multiplexer_9_out, sb;
  wire [15:0] multiplexer_8_out, sh;
  wire [23:0] Addr24;
  wire [31:0] bit_extender_3_out, bit_extender_4_out, bit_extender_5_out, bit_extender_6_out, \byte , half,
       MemWord, sbToMem, shToMem;

  // Probe on A
  // Probe on WD
  Decoder #(.select(2), .disabled(0), .enable("false")) decoder_1 (
    .out0(decoder_1_out0), .out1(decoder_1_out1), .out2(decoder_1_out2), .out3(decoder_1_out3),
    .sel(offset_byte));
  Multiplexer #(.select(2), .width(32), .disabled(0), .enable("false")) multiplexer_1 (
    .in0(WD), .in1(shToMem), .in2(sbToMem), .out(WT), .sel(size));  // open: in3
  Decoder #(.disabled(0), .enable("false")) decoder_2 (.out0(decoder_2_out0), .out1(decoder_2_out1), .sel(offset_half));
  Multiplexer #(.width(8), .disabled(0), .enable("false")) multiplexer_2 (
    .in0(MemWord[7:0]), .in1(sb), .out(sbToMem[7:0]), .sel(decoder_1_out0));
  Multiplexer #(.width(8), .disabled(0), .enable("false")) multiplexer_3 (
    .in0(MemWord[23:16]), .in1(sb), .out(sbToMem[23:16]), .sel(decoder_1_out2));
  Multiplexer #(.width(16), .disabled(0), .enable("false")) multiplexer_4 (
    .in0(MemWord[15:0]), .in1(sh), .out(shToMem[15:0]), .sel(decoder_2_out0));
  Multiplexer #(.width(16), .disabled(0), .enable("false")) multiplexer_5 (
    .in0(MemWord[31:16]), .in1(sh), .out(shToMem[31:16]), .sel(decoder_2_out1));
  Pull_Resistor pull_resistor_1 (.node(size));
  dm_addr24 dm_addr24_1 (.Addr32(A), .Addr24(Addr24), .offset_byte(offset_byte), .offset_half(offset_half));
  Multiplexer #(.width(8), .disabled(0), .enable("false")) multiplexer_6 (
    .in0(MemWord[15:8]), .in1(sb), .out(sbToMem[15:8]), .sel(decoder_1_out1));
  Multiplexer #(.width(8), .disabled(0), .enable("false")) multiplexer_7 (
    .in0(MemWord[31:24]), .in1(sb), .out(sbToMem[31:24]), .sel(decoder_1_out3));
  Pull_Resistor pull_resistor_2 (.node(extop));
  Bit_Extender #(.in_width(32)) bit_extender_1 (.in(WD), .out(sh));
  Bit_Extender #(.in_width(32), .out_width(8)) bit_extender_2 (.in(WD), .out(sb));
  RAM #(.addrWidth(24), .dataWidth(32), .bus("separate")) ram_1 (
    .addr(Addr24), .din(WT), .data(MemWord), .str(WE), .sel(1'b1), .clk(clk), .ld(1'b1), .clr(rst));
  assign bit_extender_3_out = {{16{1'b0}}, multiplexer_8_out};  // Bit_Extender bit_extender_3
  Multiplexer #(.width(16), .disabled(0), .enable("false")) multiplexer_8 (
    .in0(MemWord[15:0]), .in1(MemWord[31:16]), .out(multiplexer_8_out), .sel(offset_half));
  assign bit_extender_4_out = {{16{multiplexer_8_out[15]}}, multiplexer_8_out};  // Bit_Extender bit_extender_4
  assign bit_extender_5_out = {{24{1'b0}}, multiplexer_9_out};  // Bit_Extender bit_extender_5
  Multiplexer #(.select(2), .width(8), .disabled(0), .enable("false")) multiplexer_9 (
    .in0(MemWord[7:0]), .in1(MemWord[15:8]), .in2(MemWord[23:16]), .in3(MemWord[31:24]),
    .out(multiplexer_9_out), .sel(offset_byte));
  assign bit_extender_6_out = {{24{multiplexer_9_out[7]}}, multiplexer_9_out};  // Bit_Extender bit_extender_6
  Multiplexer #(.width(32), .disabled(0), .enable("false")) multiplexer_10 (
    .in0(bit_extender_3_out), .in1(bit_extender_4_out), .out(half), .sel(extop));
  Multiplexer #(.width(32), .disabled(0), .enable("false")) multiplexer_11 (
    .in0(bit_extender_5_out), .in1(bit_extender_6_out), .out(\byte ), .sel(extop));
  Multiplexer #(.select(2), .width(32), .disabled(0), .enable("false")) multiplexer_12 (
    .in0(MemWord), .in1(half), .in2(\byte ), .out(RD), .sel(size));  // open: in3
  Bit_Extender #(.in_width(24), .out_width(5)) bit_extender_7 (.in(Addr24), .out(WAddr5));

  // Other names for the same wires on the sheet: WordToMem[31:0] = WT

  // Notes on the sheet:
  //   Data Memory 数据存储器
  //   clk:时钟，rst:异步重置
  //   A: 地址，WD: 要写入的数据
  //   WE: 写使能(1可写0不写)
  //   size: 读写的大小规模(00字，01半字，10字节，11留空)
  //   extop: 符号扩展类型(1有符号0无符号)，仅在读半字和字节时有效
  //   根据要写入的字或者字节与内存中原有的部分进行拼接
  //   确定要向内存中写入的字
  //   从寄存器取出字或者字节
  //   24位的DM，供自己课下使用
  //   根据字和偏移量取出相应的字节或半字并进行扩展
endmodule

module dm_addr24 (
  input  [31:0] Addr32,
  output [23:0] Addr24,
  output [1:0] offset_byte,
  output offset_half
);

  wire [31:0] shifter_1_out;

  Shifter_part #(.width(32), .shift("lr")) shifter_1 (.in(Addr32), .\dist (5'b00010), .out(shifter_1_out));
  Bit_Extender #(.in_width(32), .out_width(24)) bit_extender_1 (.in(shifter_1_out), .out(Addr24));

  assign offset_byte = Addr32[1:0];
  assign offset_half = Addr32[1];

  // Notes on the sheet:
  //   dm_addr: 将DM的32位输入地址转化成24位的RAM地址
endmodule

module dm_addr5 (
  input  [31:0] Addr32,
  output [4:0] Addr5,
  output [1:0] offset_byte,
  output offset_half
);

  wire [31:0] shifter_1_out;

  Shifter_part #(.width(32), .shift("lr")) shifter_1 (.in(Addr32), .\dist (5'b00010), .out(shifter_1_out));
  Bit_Extender #(.in_width(32), .out_width(5)) bit_extender_1 (.in(shifter_1_out), .out(Addr5));

  assign offset_byte = Addr32[1:0];
  assign offset_half = Addr32[1];

  // Notes on the sheet:
  //   dm_addr5: 将DM的32位输入地址转化成5位的RAM地址
endmodule

module Control (
  input  [5:0] opcode,
  input  [5:0] funct,
  input  [4:0] rs,
  input  [4:0] rt,
  output Branch,
  output [3:0] BRop,
  output Jump,
  output JmpSrc,
  output EXTop,
  output BRspc,
  output ALUsrc,
  output [3:0] ALUop,
  output SHsrc,
  output [2:0] SHop,
  output CALCsrc,
  output MemWrite,
  output [1:0] Dsize,
  output Dext,
  output RegWrite,
  output [1:0] RegDst,
  output MemtoReg,
  output JmpLnk
);

  wire add, addi, addiu, addu, \and , andi, beq, bgez, bgtz, blez, bltz, bne, equ_5_1_equal, equ_5_2_equal,
       i_arith, j, jal, jalr, jr, lb, lbu, lh, lhu, lui, lw, mem_rw, nop, \nor , \or , or_7_out, or_8_out,
       or_9_out, or_10_out, or_11_out, or_12_out, or_13_out, or_14_out, or_15_out, or_19_out, or_20_out,
       or_21_out, or_27_out, or_28_out, orgate_8_2_out, ori, r_arith, sb, sh, sll, sllv, slt, slti, sltiu,
       sltu, sra, srav, srl, srlv, sub, subu, sw, \xor , xori;

  Pull_Resistor pull_resistor_1 (.node(opcode));
  Pull_Resistor pull_resistor_2 (.node(funct));
  Pull_Resistor pull_resistor_3 (.node(rs));
  Pull_Resistor pull_resistor_4 (.node(rt));
  instr_judger instr_judger_1 (
    .op(opcode), .op_std({6{1'b0}}), .op_en(1'b1), .funct(funct), .funct_std(6'b100000), .funct_en(1'b1),
    .correct(add));
  instr_judger instr_judger_2 (
    .op(opcode), .op_std({6{1'b0}}), .op_en(1'b1), .funct(funct), .funct_std(6'b100010), .funct_en(1'b1),
    .correct(sub));
  instr_judger instr_judger_3 (
    .op(opcode), .op_std({6{1'b0}}), .op_en(1'b1), .funct(funct), .funct_std(6'b100001), .funct_en(1'b1),
    .correct(addu));
  instr_judger instr_judger_4 (
    .op(opcode), .op_std({6{1'b0}}), .op_en(1'b1), .funct(funct), .funct_std(6'b100011), .funct_en(1'b1),
    .correct(subu));
  instr_judger instr_judger_5 (
    .op(opcode), .op_std({6{1'b0}}), .op_en(1'b1), .funct(funct), .funct_std(6'b100100), .funct_en(1'b1),
    .correct(\and ));
  instr_judger instr_judger_6 (
    .op(opcode), .op_std({6{1'b0}}), .op_en(1'b1), .funct(funct), .funct_std(6'b100101), .funct_en(1'b1),
    .correct(\or ));
  instr_judger instr_judger_7 (
    .op(opcode), .op_std({6{1'b0}}), .op_en(1'b1), .funct(funct), .funct_std(6'b100110), .funct_en(1'b1),
    .correct(\xor ));
  instr_judger instr_judger_8 (
    .op(opcode), .op_std({6{1'b0}}), .op_en(1'b1), .funct(funct), .funct_std(6'b100111), .funct_en(1'b1),
    .correct(\nor ));
  instr_judger instr_judger_9 (
    .op(opcode), .op_std({6{1'b0}}), .op_en(1'b1), .funct(funct), .funct_std(6'b101010), .funct_en(1'b1),
    .correct(slt));
  instr_judger instr_judger_10 (
    .op(opcode), .op_std({6{1'b0}}), .op_en(1'b1), .funct(funct), .funct_std(6'b101011), .funct_en(1'b1),
    .correct(sltu));
  or or_1 (JmpSrc, jalr, jr);
  Pull_Resistor pull_resistor_5 (.node(BRop));
  Priority_Encoder #(.select(4)) priority_encoder_1 (
    .in0(beq), .in1(bne), .in2(bgez), .in3(bgtz), .in4(blez), .in5(bltz), .out(BRop));  // open: in6, in7, in8, in9, in10, in11, in12, in13, in14, in15, gs, en_out, en_in
  or or_2 (r_arith, add, sub, addu, subu, \and , \or , \xor , \nor , slt, sltu);
  instr_judger instr_judger_11 (
    .op(opcode), .op_std({6{1'b0}}), .op_en(1'b1), .funct(funct), .funct_std({6{1'b0}}), .funct_en(1'b1),
    .correct(sll));
  instr_judger instr_judger_12 (
    .op(opcode), .op_std({6{1'b0}}), .op_en(1'b1), .funct(funct), .funct_std(6'b000010), .funct_en(1'b1),
    .correct(srl));
  instr_judger instr_judger_13 (
    .op(opcode), .op_std({6{1'b0}}), .op_en(1'b1), .funct(funct), .funct_std(6'b000011), .funct_en(1'b1),
    .correct(sra));
  instr_judger instr_judger_14 (
    .op(opcode), .op_std({6{1'b0}}), .op_en(1'b1), .funct(funct), .funct_std(6'b000100), .funct_en(1'b1),
    .correct(sllv));
  instr_judger instr_judger_15 (
    .op(opcode), .op_std({6{1'b0}}), .op_en(1'b1), .funct(funct), .funct_std(6'b000110), .funct_en(1'b1),
    .correct(srlv));
  instr_judger instr_judger_16 (
    .op(opcode), .op_std({6{1'b0}}), .op_en(1'b1), .funct(funct), .funct_std(6'b000111), .funct_en(1'b1),
    .correct(srav));
  or or_3 (CALCsrc, sll, srl, sra, sllv, srlv, srav);
  orgate_8 orgate_8_1 (
    .In0(addi), .In1(addiu), .In2(slti), .In3(sltiu), .In6(mem_rw), .In7(Branch), .out(EXTop));  // open: In4, In5
  instr_judger instr_judger_17 (
    .op(opcode), .op_std(6'b001000), .op_en(1'b1), .funct(funct), .funct_std({6{1'b0}}), .funct_en(1'b0),
    .correct(addi));
  instr_judger instr_judger_18 (
    .op(opcode), .op_std(6'b001111), .op_en(1'b1), .funct(funct), .funct_std({6{1'b0}}), .funct_en(1'b0),
    .correct(lui));
  instr_judger instr_judger_19 (
    .op(opcode), .op_std(6'b001101), .op_en(1'b1), .funct(funct), .funct_std({6{1'b0}}), .funct_en(1'b0),
    .correct(ori));
  instr_judger instr_judger_20 (
    .op(opcode), .op_std(6'b001001), .op_en(1'b1), .funct(funct), .funct_std({6{1'b0}}), .funct_en(1'b0),
    .correct(addiu));
  instr_judger instr_judger_21 (
    .op(opcode), .op_std(6'b001100), .op_en(1'b1), .funct(funct), .funct_std({6{1'b0}}), .funct_en(1'b0),
    .correct(andi));
  instr_judger instr_judger_22 (
    .op(opcode), .op_std(6'b001110), .op_en(1'b1), .funct(funct), .funct_std({6{1'b0}}), .funct_en(1'b0),
    .correct(xori));
  instr_judger instr_judger_23 (
    .op(opcode), .op_std(6'b001010), .op_en(1'b1), .funct(funct), .funct_std({6{1'b0}}), .funct_en(1'b0),
    .correct(slti));
  instr_judger instr_judger_24 (
    .op(opcode), .op_std(6'b001011), .op_en(1'b1), .funct(funct), .funct_std({6{1'b0}}), .funct_en(1'b0),
    .correct(sltiu));
  // instr_judger instr_judger_25: pin names not known; wires that end beside it: opcode, {6{1'b0}}, 1'b1, funct, {6{1'b0}}, 1'b1, nop
  or or_4 (i_arith, addi, lui, ori, addiu, andi, xori, slti, sltiu);
  orgate_8 orgate_8_2 (
    .In0(mem_rw), .In2(add), .In3(addi), .In4(addu), .In5(addiu), .out(orgate_8_2_out));  // open: In1, In6, In7
  instr_judger instr_judger_26 (
    .op(opcode), .op_std(6'b101011), .op_en(1'b1), .funct(funct), .funct_std({6{1'b0}}), .funct_en(1'b0),
    .correct(sw));
  instr_judger instr_judger_27 (
    .op(opcode), .op_std(6'b100011), .op_en(1'b1), .funct(funct), .funct_std({6{1'b0}}), .funct_en(1'b0),
    .correct(lw));
  instr_judger instr_judger_28 (
    .op(opcode), .op_std(6'b101000), .op_en(1'b1), .funct(funct), .funct_std({6{1'b0}}), .funct_en(1'b0),
    .correct(sb));
  instr_judger instr_judger_29 (
    .op(opcode), .op_std(6'b101001), .op_en(1'b1), .funct(funct), .funct_std({6{1'b0}}), .funct_en(1'b0),
    .correct(sh));
  instr_judger instr_judger_30 (
    .op(opcode), .op_std(6'b100000), .op_en(1'b1), .funct(funct), .funct_std({6{1'b0}}), .funct_en(1'b0),
    .correct(lb));
  instr_judger instr_judger_31 (
    .op(opcode), .op_std(6'b100001), .op_en(1'b1), .funct(funct), .funct_std({6{1'b0}}), .funct_en(1'b0),
    .correct(lh));
  instr_judger instr_judger_32 (
    .op(opcode), .op_std(6'b100100), .op_en(1'b1), .funct(funct), .funct_std({6{1'b0}}), .funct_en(1'b0),
    .correct(lbu));
  instr_judger instr_judger_33 (
    .op(opcode), .op_std(6'b100101), .op_en(1'b1), .funct(funct), .funct_std({6{1'b0}}), .funct_en(1'b0),
    .correct(lhu));
  or or_5 (ALUsrc, i_arith, mem_rw);
  or or_6 (SHsrc, sllv, srlv, srav);
  or or_7 (or_7_out, sub, subu);
  or or_8 (or_8_out, \and , andi);
  or or_9 (or_9_out, \or , ori);
  or or_10 (or_10_out, \xor , xori);
  or or_11 (or_11_out, slt, slti);
  or or_12 (or_12_out, sltu, sltiu);
  or or_13 (or_13_out, sll, sllv);
  or or_14 (or_14_out, srl, srlv);
  or or_15 (or_15_out, sra, srav);
  Priority_Encoder #(.select(4)) priority_encoder_2 (
    .in0(orgate_8_2_out), .in1(or_7_out), .in2(or_8_out), .in3(or_9_out), .in4(\nor ), .in5(or_10_out),
    .in6(or_11_out), .in7(or_12_out), .in8(lui), .out(ALUop));  // open: in9, in10, in11, in12, in13, in14, in15, gs, en_out, en_in
  Pull_Resistor pull_resistor_6 (.node(ALUop));
  Priority_Encoder priority_encoder_3 (
    .in0(or_13_out), .in1(or_14_out), .in2(or_15_out), .out(SHop));  // open: in3, in4, in5, in6, in7, en_in, gs, en_out
  Pull_Resistor pull_resistor_7 (.node(SHop));
  instr_judger instr_judger_34 (
    .op(opcode), .op_std(6'b000100), .op_en(1'b1), .funct(funct), .funct_std({6{1'b0}}), .funct_en(1'b0),
    .correct(beq));
  instr_judger instr_judger_35 (
    .op(opcode), .op_std(6'b000101), .op_en(1'b1), .funct(funct), .funct_std({6{1'b0}}), .funct_en(1'b0),
    .correct(bne));
  instr_judger instr_judger_36 (
    .op(opcode), .op_std(6'b000111), .op_en(1'b1), .funct(funct), .funct_std({6{1'b0}}), .funct_en(1'b0),
    .correct(bgtz));
  instr_judger instr_judger_37 (
    .op(opcode), .op_std(6'b000110), .op_en(1'b1), .funct(funct), .funct_std({6{1'b0}}), .funct_en(1'b0),
    .correct(blez));
  instr_judger instr_judger_38 (
    .op(opcode), .op_std(6'b000001), .op_en(1'b1), .funct(funct), .funct_std({6{1'b0}}), .funct_en(1'b0),
    .correct(BRspc));
  and and_1 (bgez, BRspc, equ_5_1_equal);
  equ_5 equ_5_1 (.A(rt), .B(5'b00001), .equal(equ_5_1_equal));
  and and_2 (bltz, BRspc, equ_5_2_equal);
  equ_5 equ_5_2 (.A(rt), .B({5{1'b0}}), .equal(equ_5_2_equal));
  or or_16 (MemtoReg, lw, lb, lh, lbu, lhu);
  or or_17 (MemWrite, sh, sb, sw);
  or or_18 (mem_rw, MemtoReg, MemWrite);
  or or_19 (or_19_out, lw, sw);
  or or_20 (or_20_out, lh, lhu, sh);
  or or_21 (or_21_out, lb, lbu, sb);
  instr_judger instr_judger_39 (
    .op(opcode), .op_std(6'b000010), .op_en(1'b1), .funct(funct), .funct_std({6{1'b0}}), .funct_en(1'b0),
    .correct(j));
  instr_judger instr_judger_40 (
    .op(opcode), .op_std(6'b000011), .op_en(1'b1), .funct(funct), .funct_std({6{1'b0}}), .funct_en(1'b0),
    .correct(jal));
  instr_judger instr_judger_41 (
    .op(opcode), .op_std({6{1'b0}}), .op_en(1'b1), .funct(funct), .funct_std(6'b001001), .funct_en(1'b1),
    .correct(jalr));
  instr_judger instr_judger_42 (
    .op(opcode), .op_std({6{1'b0}}), .op_en(1'b1), .funct(funct), .funct_std(6'b001000), .funct_en(1'b1),
    .correct(jr));
  or or_22 (Branch, beq, bne, bgtz, blez, bgez, bltz);
  Priority_Encoder #(.select(2)) priority_encoder_4 (
    .in0(or_19_out), .in1(or_20_out), .in2(or_21_out), .out(Dsize));  // open: in3, gs, en_out, en_in
  Pull_Resistor pull_resistor_8 (.node(Dsize));
  or or_23 (Dext, lb, lw, lh);
  or or_24 (Jump, j, jal, jalr, jr);
  or or_25 (RegWrite, r_arith, CALCsrc, JmpLnk, i_arith, MemtoReg);
  or or_26 (JmpLnk, jal, jalr);
  or or_27 (or_27_out, r_arith, jalr, CALCsrc);
  or or_28 (or_28_out, i_arith, MemtoReg);
  Pull_Resistor pull_resistor_9 (.node(RegDst));
  Priority_Encoder #(.select(2)) priority_encoder_5 (
    .in0(or_27_out), .in1(or_28_out), .in2(jal), .out(RegDst));  // open: in3, gs, en_out, en_in

  // Other names for the same wires on the sheet: b_special = BRspc; mem_r = MemtoReg; mem_w = MemWrite;
  //   r_shift = CALCsrc

  // Notes on the sheet:
  //   Control Unit: CPU的控制器单元
  //   加指令方法：复制一个instr模块，修改opcode和funct的常量以及输出的标签即可
  //   R型运算指令
  //   R型运算指令
  //   取指阶段
  //   移位指令
  //   移位指令
  //   指令种类判断区
  //   译码阶段
  //   I型运算指令
  //   指令分类区(中间分类)
  //   I型运算指令
  //   输出信号生成区
  //   内存读写
  //   执行阶段
  //   条件分支
  //   内存读写
  //   条件分支
  //   跳转
  //   访存阶段
  //   跳转
  //   输出信号区
  //   取指阶段
  //   译码阶段
  //   执行阶段
  //   访存阶段
  //   回写阶段
  //   回写阶段
endmodule

module equ_5 (
  input  [4:0] A,
  input  [4:0] B,
  output equal
);

  wire [4:0] xor_1_out;

  Pull_Resistor pull_resistor_1 (.node(A));
  Pull_Resistor pull_resistor_2 (.node(B));
  assign xor_1_out = A ^ B;  // XOR_Gate xor_1, 5 bits wide
  nor nor_1 (equal, xor_1_out[0], xor_1_out[1], xor_1_out[2], xor_1_out[3], xor_1_out[4]);
endmodule

module equ_6 (
  input  [5:0] A,
  input  [5:0] B,
  output equal
);

  wire [5:0] xor_1_out;

  Pull_Resistor pull_resistor_1 (.node(A));
  Pull_Resistor pull_resistor_2 (.node(B));
  assign xor_1_out = A ^ B;  // XOR_Gate xor_1, 6 bits wide
  nor nor_1 (equal, xor_1_out[0], xor_1_out[1], xor_1_out[2], xor_1_out[3], xor_1_out[4], xor_1_out[5]);
endmodule

module instr_judger (
  input  [5:0] op,
  input  [5:0] op_std,
  input  op_en,
  input  [5:0] funct,
  input  [5:0] funct_std,
  input  funct_en,
  output correct
);

  wire equ_6_1_equal, equ_6_2_equal, or_1_out, or_2_out;

  equ_6 equ_6_1 (.A(op), .B(op_std), .equal(equ_6_1_equal));
  equ_6 equ_6_2 (.A(funct), .B(funct_std), .equal(equ_6_2_equal));
  or or_1 (or_1_out, equ_6_1_equal, ~op_en);  // OR_Gate
  or or_2 (or_2_out, equ_6_2_equal, ~funct_en);  // OR_Gate
  and and_1 (correct, or_1_out, or_2_out);

  // Notes on the sheet:
  //   指令判断器：根据给定的opcode和funct判断一条指令是不是某指令
  //   op: 输入指令的op，op_std: 要判断是不是的指令的op，op_en: 是否检查op一致
  //   输出：是否为某指令
  //   例如：将op_std设定为0，funct_std设定为100000，若输入的op和funct一致则该指令为add指令
  //   下面的funct同理
  //   使用方法：op以及funct连接模块输入的op和funct
  //   两路en信号是以备万一某些指令只有op确定而funct任意，可以不判断funct
  //   op_std, funct_std用常量
  //   （例如I型和J型指令，funct对应的位数都是立即数，没意义）
endmodule

module big_andgate_32 (
  input  in_1,
  input  in_2,
  input  in_3,
  input  in_4,
  input  in_5,
  input  in_6,
  input  in_7,
  input  in_8,
  input  in_9,
  input  in_10,
  input  in_11,
  input  in_12,
  input  in_13,
  input  in_14,
  input  in_15,
  input  in_16,
  input  in_17,
  input  in_18,
  input  in_19,
  input  in_20,
  input  in_21,
  input  in_22,
  input  in_23,
  input  in_24,
  input  in_25,
  input  in_26,
  input  in_27,
  input  in_28,
  input  in_29,
  input  in_30,
  input  in_31,
  input  in_32,
  output out_33
);

  Pull_Resistor pull_resistor_1 (.node(in_1));
  Pull_Resistor pull_resistor_2 (.node(in_9));
  Pull_Resistor pull_resistor_3 (.node(in_17));
  Pull_Resistor pull_resistor_4 (.node(in_25));
  Pull_Resistor pull_resistor_5 (.node(in_2));
  Pull_Resistor pull_resistor_6 (.node(in_10));
  Pull_Resistor pull_resistor_7 (.node(in_18));
  Pull_Resistor pull_resistor_8 (.node(in_26));
  Pull_Resistor pull_resistor_9 (.node(in_3));
  Pull_Resistor pull_resistor_10 (.node(in_11));
  Pull_Resistor pull_resistor_11 (.node(in_19));
  Pull_Resistor pull_resistor_12 (.node(in_27));
  Pull_Resistor pull_resistor_13 (.node(in_4));
  Pull_Resistor pull_resistor_14 (.node(in_12));
  Pull_Resistor pull_resistor_15 (.node(in_20));
  Pull_Resistor pull_resistor_16 (.node(in_28));
  Pull_Resistor pull_resistor_17 (.node(in_5));
  Pull_Resistor pull_resistor_18 (.node(in_6));
  Pull_Resistor pull_resistor_19 (.node(in_14));
  Pull_Resistor pull_resistor_20 (.node(in_13));
  Pull_Resistor pull_resistor_21 (.node(in_22));
  Pull_Resistor pull_resistor_22 (.node(in_21));
  Pull_Resistor pull_resistor_23 (.node(in_29));
  Pull_Resistor pull_resistor_24 (.node(in_30));
  Pull_Resistor pull_resistor_25 (.node(in_7));
  Pull_Resistor pull_resistor_26 (.node(in_15));
  Pull_Resistor pull_resistor_27 (.node(in_23));
  Pull_Resistor pull_resistor_28 (.node(in_31));
  Pull_Resistor pull_resistor_29 (.node(in_8));
  Pull_Resistor pull_resistor_30 (.node(in_16));
  Pull_Resistor pull_resistor_31 (.node(in_24));
  Pull_Resistor pull_resistor_32 (.node(in_32));
  and and_1 (out_33, in_1, in_2, in_3, in_4, in_5, in_6, in_7, in_8, in_9, in_10, in_11, in_12, in_13, in_14, in_15, in_16, in_17, in_18, in_19, in_20, in_21, in_22, in_23, in_24, in_25, in_26, in_27, in_28, in_29, in_30, in_31, in_32);

  // Notes on the sheet:
  //   在控制单元这里定制的专用与门，自带32路1位输入，所有的X输入自动下拉为0，不影响有输入的端。全X则输出0
endmodule

module big_orgate_32 (
  input  in_1,
  input  in_2,
  input  in_3,
  input  in_4,
  input  in_5,
  input  in_6,
  input  in_7,
  input  in_8,
  input  in_9,
  input  in_10,
  input  in_11,
  input  in_12,
  input  in_13,
  input  in_14,
  input  in_15,
  input  in_16,
  input  in_17,
  input  in_18,
  input  in_19,
  input  in_20,
  input  in_21,
  input  in_22,
  input  in_23,
  input  in_24,
  input  in_25,
  input  in_26,
  input  in_27,
  input  in_28,
  input  in_29,
  input  in_30,
  input  in_31,
  input  in_32,
  output out_33
);

  Pull_Resistor pull_resistor_1 (.node(in_1));
  Pull_Resistor pull_resistor_2 (.node(in_9));
  Pull_Resistor pull_resistor_3 (.node(in_17));
  Pull_Resistor pull_resistor_4 (.node(in_25));
  Pull_Resistor pull_resistor_5 (.node(in_2));
  Pull_Resistor pull_resistor_6 (.node(in_10));
  Pull_Resistor pull_resistor_7 (.node(in_18));
  Pull_Resistor pull_resistor_8 (.node(in_26));
  Pull_Resistor pull_resistor_9 (.node(in_3));
  Pull_Resistor pull_resistor_10 (.node(in_11));
  Pull_Resistor pull_resistor_11 (.node(in_19));
  Pull_Resistor pull_resistor_12 (.node(in_27));
  Pull_Resistor pull_resistor_13 (.node(in_4));
  Pull_Resistor pull_resistor_14 (.node(in_12));
  Pull_Resistor pull_resistor_15 (.node(in_20));
  Pull_Resistor pull_resistor_16 (.node(in_28));
  Pull_Resistor pull_resistor_17 (.node(in_6));
  Pull_Resistor pull_resistor_18 (.node(in_5));
  Pull_Resistor pull_resistor_19 (.node(in_13));
  Pull_Resistor pull_resistor_20 (.node(in_14));
  Pull_Resistor pull_resistor_21 (.node(in_21));
  Pull_Resistor pull_resistor_22 (.node(in_22));
  Pull_Resistor pull_resistor_23 (.node(in_30));
  Pull_Resistor pull_resistor_24 (.node(in_29));
  Pull_Resistor pull_resistor_25 (.node(in_7));
  Pull_Resistor pull_resistor_26 (.node(in_15));
  Pull_Resistor pull_resistor_27 (.node(in_23));
  Pull_Resistor pull_resistor_28 (.node(in_31));
  Pull_Resistor pull_resistor_29 (.node(in_8));
  Pull_Resistor pull_resistor_30 (.node(in_16));
  Pull_Resistor pull_resistor_31 (.node(in_24));
  Pull_Resistor pull_resistor_32 (.node(in_32));
  or or_1 (out_33, in_1, in_2, in_3, in_4, in_5, in_6, in_7, in_8, in_9, in_10, in_11, in_12, in_13, in_14, in_15, in_16, in_17, in_18, in_19, in_20, in_21, in_22, in_23, in_24, in_25, in_26, in_27, in_28, in_29, in_30, in_31, in_32);

  // Notes on the sheet:
  //   在控制单元这里定制的专用或门，自带32路1位输入，所有的X输入自动下拉为0，不影响有输入的端。全X则输出0
endmodule

module andgate_8 (
  input  In0,
  input  In1,
  input  In2,
  input  In3,
  input  In4,
  input  In5,
  input  In6,
  input  In7,
  output out
);

  Pull_Resistor pull_resistor_1 (.node(In0));
  Pull_Resistor pull_resistor_2 (.node(In1));
  Pull_Resistor pull_resistor_3 (.node(In2));
  Pull_Resistor pull_resistor_4 (.node(In5));
  Pull_Resistor pull_resistor_5 (.node(In4));
  Pull_Resistor pull_resistor_6 (.node(In3));
  Pull_Resistor pull_resistor_7 (.node(In6));
  Pull_Resistor pull_resistor_8 (.node(In7));
  and and_1 (out, In0, In1, In2, In3, In4, In5, In6, In7);
endmodule

module orgate_8 (
  input  In0,
  input  In1,
  input  In2,
  input  In3,
  input  In4,
  input  In5,
  input  In6,
  input  In7,
  output out
);

  Pull_Resistor pull_resistor_1 (.node(In0));
  Pull_Resistor pull_resistor_2 (.node(In1));
  Pull_Resistor pull_resistor_3 (.node(In4));
  Pull_Resistor pull_resistor_4 (.node(In5));
  Pull_Resistor pull_resistor_5 (.node(In2));
  Pull_Resistor pull_resistor_6 (.node(In3));
  Pull_Resistor pull_resistor_7 (.node(In6));
  Pull_Resistor pull_resistor_8 (.node(In7));
  or or_1 (out, In0, In1, In2, In3, In4, In5, In6, In7);
endmodule
