// Logisim project Control.circ as structural Verilog: 7 circuits, main circuit Control
module Control (
  input  [5:0] opcode,
  input  [5:0] funct,
  input  [4:0] rs,
  input  [4:0] rt,
  output MemtoReg,
  output MemWrite,
  output RegWrite,
  output [1:0] RegDst,
  output [1:0] Msize,
  output Mext,
  output [3:0] ALUop,
  output EXTop,
  output ALUsrc,
  output Shift,
  output [2:0] SHop,
  output SHsrc,
  output Branch,
  output [3:0] BRop,
  output BRspc,
  output Jump,
  output JmpSrc,
  output JmpLnk
);

  wire _arith, _arith_i, _arith_r, _mem, add, addi, addiu, addu, \and , andi, beq, bgez, bgtz, blez, bltz,
       bne, equ_checker_5_1_equal, equ_checker_5_2_equal, j, jal, jalr, jr, lb, lbu, lh, lhu, lui, lw, nop,
       \nor , \or , or_4_out, or_5_out, or_6_out, or_7_out, or_8_out, or_9_out, or_10_out, or_11_out,
       or_12_out, or_13_out, or_14_out, or_15_out, or_16_out, or_20_out, or_21_out, or_22_out, or_23_out,
       or_24_out, orgate_8_1_out, orgate_8_2_out, orgate_8_4_out, ori, sb, sh, sll, sllv, slt, slti, sltiu,
       sltu, sra, srav, srl, srlv, sub, subu, sw, \xor , xori;

  Pull_Resistor pull_resistor_1 (.node(opcode));
  Pull_Resistor pull_resistor_2 (.node(funct));
  Pull_Resistor pull_resistor_3 (.node(rs));
  Pull_Resistor pull_resistor_4 (.node(rt));
  instr_judger instr_judger_1 (
    .op(opcode), .op_std({6{1'b0}}), .op_en(1'b1), .funct(funct), .funct_std(6'b100000), .funct_en(1'b1),
    .correct(add));
  instr_judger instr_judger_2 (
    .op(opcode), .op_std({6{1'b0}}), .op_en(1'b1), .funct(funct), .funct_std(6'b100010), .funct_en(1'b1),
    .correct(sub));
  instr_judger instr_judger_3 (
    .op(opcode), .op_std({6{1'b0}}), .op_en(1'b1), .funct(funct), .funct_std(6'b100001), .funct_en(1'b1),
    .correct(addu));
  instr_judger instr_judger_4 (
    .op(opcode), .op_std({6{1'b0}}), .op_en(1'b1), .funct(funct), .funct_std(6'b100011), .funct_en(1'b1),
    .correct(subu));
  instr_judger instr_judger_5 (
    .op(opcode), .op_std({6{1'b0}}), .op_en(1'b1), .funct(funct), .funct_std(6'b100100), .funct_en(1'b1),
    .correct(\and ));
  instr_judger instr_judger_6 (
    .op(opcode), .op_std({6{1'b0}}), .op_en(1'b1), .funct(funct), .funct_std(6'b100101), .funct_en(1'b1),
    .correct(\or ));
  instr_judger instr_judger_7 (
    .op(opcode), .op_std({6{1'b0}}), .op_en(1'b1), .funct(funct), .funct_std(6'b100110), .funct_en(1'b1),
    .correct(\xor ));
  instr_judger instr_judger_8 (
    .op(opcode), .op_std({6{1'b0}}), .op_en(1'b1), .funct(funct), .funct_std(6'b100111), .funct_en(1'b1),
    .correct(\nor ));
  instr_judger instr_judger_9 (
    .op(opcode), .op_std({6{1'b0}}), .op_en(1'b1), .funct(funct), .funct_std(6'b101010), .funct_en(1'b1),
    .correct(slt));
  instr_judger instr_judger_10 (
    .op(opcode), .op_std({6{1'b0}}), .op_en(1'b1), .funct(funct), .funct_std(6'b101011), .funct_en(1'b1),
    .correct(sltu));
  or or_1 (MemtoReg, lw, lb, lh, lbu, lhu);
  or or_2 (MemWrite, sw, sb, sh);
  or or_3 (_mem, MemtoReg, MemWrite);
  orgate_8 orgate_8_1 (
    .In0(add), .In1(addu), .In2(addi), .In7(_mem), .out(orgate_8_1_out));  // open: In3, In4, In5, In6
  orgate_8 orgate_8_2 (.In1(subu), .In3(sub), .In7(Branch), .out(orgate_8_2_out));  // open: In0, In2, In4, In5, In6
  orgate_8 orgate_8_3 (.In0(_mem), .In7(_arith_i), .out(ALUsrc));  // open: In1, In2, In3, In4, In5, In6
  or or_4 (or_4_out, sw, lw);
  or or_5 (or_5_out, sh, lh, lhu);
  or or_6 (or_6_out, sb, lb, lbu);
  or or_7 (or_7_out, \and , andi);
  or or_8 (or_8_out, \or , ori);
  or or_9 (or_9_out, \xor , xori);
  or or_10 (or_10_out, slt, slti);
  or or_11 (or_11_out, sltiu, sltu);
  or or_12 (or_12_out, Shift, jalr, _arith_r);
  or or_13 (or_13_out, _arith_i, MemtoReg);
  Pull_Resistor pull_resistor_5 (.node(Msize));
  Priority_Encoder #(.select(2), .disabled(0)) priority_encoder_1 (
    .in0(or_4_out), .in1(or_5_out), .in2(or_6_out), .out(Msize));  // open: in3, gs, en_out, en_in
  instr_judger instr_judger_11 (
    .op(opcode), .op_std(6'b001000), .op_en(1'b1), .funct(funct), .funct_std({6{1'b0}}), .funct_en(1'b0),
    .correct(addi));
  instr_judger instr_judger_12 (
    .op(opcode), .op_std(6'b001111), .op_en(1'b1), .funct(funct), .funct_std({6{1'b0}}), .funct_en(1'b0),
    .correct(lui));
  instr_judger instr_judger_13 (
    .op(opcode), .op_std(6'b001101), .op_en(1'b1), .funct(funct), .funct_std({6{1'b0}}), .funct_en(1'b0),
    .correct(ori));
  instr_judger instr_judger_14 (
    .op(opcode), .op_std(6'b001001), .op_en(1'b1), .funct(funct), .funct_std({6{1'b0}}), .funct_en(1'b0),
    .correct(addiu));
  instr_judger instr_judger_15 (
    .op(opcode), .op_std(6'b001100), .op_en(1'b1), .funct(funct), .funct_std({6{1'b0}}), .funct_en(1'b0),
    .correct(andi));
  instr_judger instr_judger_16 (
    .op(opcode), .op_std(6'b001110), .op_en(1'b1), .funct(funct), .funct_std({6{1'b0}}), .funct_en(1'b0),
    .correct(xori));
  instr_judger instr_judger_17 (
    .op(opcode), .op_std(6'b001010), .op_en(1'b1), .funct(funct), .funct_std({6{1'b0}}), .funct_en(1'b0),
    .correct(slti));
  instr_judger instr_judger_18 (
    .op(opcode), .op_std(6'b001011), .op_en(1'b1), .funct(funct), .funct_std({6{1'b0}}), .funct_en(1'b0),
    .correct(sltiu));
  or or_14 (or_14_out, add, addu);
  or or_15 (or_15_out, sub, subu);
  or or_16 (or_16_out, slt, sltu);
  orgate_8 orgate_8_4 (.In0(ori), .In1(andi), .In2(xori), .out(orgate_8_4_out));  // open: In3, In4, In5, In6, In7
  or or_17 (RegWrite, JmpLnk, MemtoReg, _arith, Shift);
  Pull_Resistor pull_resistor_6 (.node(RegDst));
  Priority_Encoder #(.select(2), .disabled(0)) priority_encoder_2 (
    .in0(or_12_out), .in1(or_13_out), .in2(jal), .out(RegDst));  // open: in3, gs, en_out, en_in
  or or_18 (Mext, lb, lh);
  instr_judger instr_judger_19 (
    .op(opcode), .op_std({6{1'b0}}), .op_en(1'b1), .funct(funct), .funct_std({6{1'b0}}), .funct_en(1'b1),
    .correct(sll));
  instr_judger instr_judger_20 (
    .op(opcode), .op_std({6{1'b0}}), .op_en(1'b1), .funct(funct), .funct_std(6'b000100), .funct_en(1'b1),
    .correct(sllv));
  or or_19 (_arith, _arith_r, _arith_i);
  orgate_8 orgate_8_5 (
    .In0(or_14_out), .In1(or_15_out), .In2(or_16_out), .In3(\and ), .In4(\or ), .In5(\xor ), .In6(\nor ),
    .out(_arith_r));  // open: In7
  Pull_Resistor pull_resistor_7 (.node(ALUop));
  Priority_Encoder #(.select(4)) priority_encoder_3 (
    .in0(orgate_8_1_out), .in1(orgate_8_2_out), .in2(or_7_out), .in3(or_8_out), .in4(\nor ), .in5(or_9_out),
    .in6(or_10_out), .in7(or_11_out), .in8(lui), .out(ALUop));  // open: in9, in10, in11, in12, in13, in14, in15, gs, en_out, en_in
  not not_1 (EXTop, orgate_8_4_out);
  instr_judger instr_judger_21 (
    .op(opcode), .op_std(6'b101011), .op_en(1'b1), .funct(funct), .funct_std({6{1'b0}}), .funct_en(1'b0),
    .correct(sw));
  instr_judger instr_judger_22 (
    .op(opcode), .op_std(6'b100011), .op_en(1'b1), .funct(funct), .funct_std({6{1'b0}}), .funct_en(1'b0),
    .correct(lw));
  instr_judger instr_judger_23 (
    .op(opcode), .op_std(6'b101000), .op_en(1'b1), .funct(funct), .funct_std({6{1'b0}}), .funct_en(1'b0),
    .correct(sb));
  instr_judger instr_judger_24 (
    .op(opcode), .op_std(6'b101001), .op_en(1'b1), .funct(funct), .funct_std({6{1'b0}}), .funct_en(1'b0),
    .correct(sh));
  instr_judger instr_judger_25 (
    .op(opcode), .op_std(6'b100000), .op_en(1'b1), .funct(funct), .funct_std({6{1'b0}}), .funct_en(1'b0),
    .correct(lb));
  instr_judger instr_judger_26 (
    .op(opcode), .op_std(6'b100001), .op_en(1'b1), .funct(funct), .funct_std({6{1'b0}}), .funct_en(1'b0),
    .correct(lh));
  instr_judger instr_judger_27 (
    .op(opcode), .op_std(6'b100100), .op_en(1'b1), .funct(funct), .funct_std({6{1'b0}}), .funct_en(1'b0),
    .correct(lbu));
  instr_judger instr_judger_28 (
    .op(opcode), .op_std(6'b100101), .op_en(1'b1), .funct(funct), .funct_std({6{1'b0}}), .funct_en(1'b0),
    .correct(lhu));
  instr_judger instr_judger_29 (
    .op(opcode), .op_std({6{1'b0}}), .op_en(1'b1), .funct(funct), .funct_std(6'b000010), .funct_en(1'b1),
    .correct(srl));
  instr_judger instr_judger_30 (
    .op(opcode), .op_std({6{1'b0}}), .op_en(1'b1), .funct(funct), .funct_std(6'b000110), .funct_en(1'b1),
    .correct(srlv));
  or or_20 (or_20_out, addi, addiu);
  or or_21 (or_21_out, slti, sltiu);
  or or_22 (or_22_out, sll, sllv);
  or or_23 (or_23_out, srl, srlv);
  or or_24 (or_24_out, sra, srav);
  or or_25 (JmpSrc, jr, jalr);
  or or_26 (JmpLnk, jal, jalr);
  // instr_judger instr_judger_31: pin names not known; wires that end beside it: opcode, {6{1'b0}}, 1'b1, funct, {6{1'b0}}, 1'b1, nop
  instr_judger instr_judger_32 (
    .op(opcode), .op_std(6'b000010), .op_en(1'b1), .funct(funct), .funct_std({6{1'b0}}), .funct_en(1'b0),
    .correct(j));
  instr_judger instr_judger_33 (
    .op(opcode), .op_std(6'b000011), .op_en(1'b1), .funct(funct), .funct_std({6{1'b0}}), .funct_en(1'b0),
    .correct(jal));
  instr_judger instr_judger_34 (
    .op(opcode), .op_std({6{1'b0}}), .op_en(1'b1), .funct(funct), .funct_std(6'b001001), .funct_en(1'b1),
    .correct(jalr));
  instr_judger instr_judger_35 (
    .op(opcode), .op_std({6{1'b0}}), .op_en(1'b1), .funct(funct), .funct_std(6'b001000), .funct_en(1'b1),
    .correct(jr));
  instr_judger instr_judger_36 (
    .op(opcode), .op_std({6{1'b0}}), .op_en(1'b1), .funct(funct), .funct_std(6'b000011), .funct_en(1'b1),
    .correct(sra));
  instr_judger instr_judger_37 (
    .op(opcode), .op_std({6{1'b0}}), .op_en(1'b1), .funct(funct), .funct_std(6'b000111), .funct_en(1'b1),
    .correct(srav));
  orgate_8 orgate_8_6 (
    .In0(or_20_out), .In1(or_21_out), .In2(lui), .In3(ori), .In4(andi), .In5(xori), .out(_arith_i));  // open: In6, In7
  Pull_Resistor pull_resistor_8 (.node(SHop));
  Priority_Encoder priority_encoder_4 (
    .in0(or_22_out), .in1(or_23_out), .in2(or_24_out), .out(SHop));  // open: in3, in4, in5, in6, in7, en_in, gs, en_out
  orgate_8 orgate_8_7 (.In0(sllv), .In1(srlv), .In2(srav), .out(SHsrc));  // open: In3, In4, In5, In6, In7
  instr_judger instr_judger_38 (
    .op(opcode), .op_std(6'b000100), .op_en(1'b1), .funct(funct), .funct_std({6{1'b0}}), .funct_en(1'b0),
    .correct(beq));
  instr_judger instr_judger_39 (
    .op(opcode), .op_std(6'b000101), .op_en(1'b1), .funct(funct), .funct_std({6{1'b0}}), .funct_en(1'b0),
    .correct(bne));
  instr_judger instr_judger_40 (
    .op(opcode), .op_std(6'b000111), .op_en(1'b1), .funct(funct), .funct_std({6{1'b0}}), .funct_en(1'b0),
    .correct(bgtz));
  instr_judger instr_judger_41 (
    .op(opcode), .op_std(6'b000110), .op_en(1'b1), .funct(funct), .funct_std({6{1'b0}}), .funct_en(1'b0),
    .correct(blez));
  instr_judger instr_judger_42 (
    .op(opcode), .op_std(6'b000001), .op_en(1'b1), .funct(funct), .funct_std({6{1'b0}}), .funct_en(1'b0),
    .correct(BRspc));
  and and_1 (bgez, BRspc, equ_checker_5_1_equal);
  equ_checker_5 equ_checker_5_1 (.A(rt), .B(5'b00001), .equal(equ_checker_5_1_equal));
  and and_2 (bltz, BRspc, equ_checker_5_2_equal);
  equ_checker_5 equ_checker_5_2 (.A(rt), .B({5{1'b0}}), .equal(equ_checker_5_2_equal));
  orgate_8 orgate_8_8 (
    .In0(sll), .In1(srl), .In2(sra), .In3(sllv), .In4(srlv), .In5(srav), .out(Shift));  // open: In6, In7
  Pull_Resistor pull_resistor_9 (.node(BRop));
  Priority_Encoder #(.select(4)) priority_encoder_5 (
    .in0(1'b0), .in1(beq), .in2(bne), .in3(bgtz), .in4(bltz), .in5(bgez), .in6(blez), .out(BRop));  // open: in7, in8, in9, in10, in11, in12, in13, in14, in15, gs, en_out, en_in
  orgate_8 orgate_8_9 (
    .In0(beq), .In1(bne), .In2(bgtz), .In3(blez), .In4(bgez), .In5(bltz), .out(Branch));  // open: In6, In7
  or or_27 (Jump, j, jr, jal, jalr);

  // Other names for the same wires on the sheet: _mem_read = MemtoReg; _mem_write = MemWrite; b_special = BRspc

  // Notes on the sheet:
  //   Control Unit: CPU的控制器单元
  //   加指令方法：复制一个instr模块，修改opcode和funct的常量以及输出的标签即可
  //   R型运算指令
  //   指令分类区(中间分类)
  //   访存类
  //   运算类输出信号
  //   访存类输出信号
  //   I型运算指令
  //   运算类
  //   输出信号逻辑区
  //   指令种类判断区
  //   内存读写
  //   移位指令
  //   跳转类输出信号
  //   跳转
  //   移位类输出信号
  //   条件分支
  //   分支类输出信号
  //   输出信号区
  //   移位类
  //   访存类
  //   运算类
  //   分支类
  //   跳转类
  //   分支类
  //   跳转类
endmodule

module equ_checker_5 (
  input  [4:0] A,
  input  [4:0] B,
  output equal
);

  wire [4:0] xor_1_out;

  Pull_Resistor pull_resistor_1 (.node(A));
  Pull_Resistor pull_resistor_2 (.node(B));
  assign xor_1_out = A ^ B;  // XOR_Gate xor_1, 5 bits wide
  nor nor_1 (equal, xor_1_out[0], xor_1_out[1], xor_1_out[2], xor_1_out[3], xor_1_out[4]);
endmodule

module instr_judger (
  input  [5:0] op,
  input  [5:0] op_std,
  input  op_en,
  input  [5:0] funct,
  input  [5:0] funct_std,
  input  funct_en,
  output correct
);

  wire nor_1_out, nor_2_out, or_1_out, or_2_out;
  wire [5:0] xor_1_out, xor_2_out;

  assign xor_1_out = op ^ op_std;  // XOR_Gate xor_1, 6 bits wide
  assign xor_2_out = funct ^ funct_std;  // XOR_Gate xor_2, 6 bits wide
  nor nor_1 (nor_1_out, xor_1_out[0], xor_1_out[1], xor_1_out[2], xor_1_out[3], xor_1_out[4], xor_1_out[5]);
  nor nor_2 (nor_2_out, xor_2_out[0], xor_2_out[1], xor_2_out[2], xor_2_out[3], xor_2_out[4], xor_2_out[5]);
  or or_1 (or_1_out, nor_1_out, ~op_en);  // OR_Gate
  or or_2 (or_2_out, nor_2_out, ~funct_en);  // OR_Gate
  and and_1 (correct, or_1_out, or_2_out);

  // Notes on the sheet:
  //   指令判断器：根据给定的opcode和funct判断一条指令是不是某指令
  //   op: 输入指令的op，op_std: 要判断是不是的指令的op，op_en: 是否检查op一致
  //   输出：是否为某指令
  //   例如：将op_std设定为0，funct_std设定为100000，若输入的op和funct一致则该指令为add指令
  //   下面的funct同理
  //   使用方法：op以及funct连接模块输入的op和funct
  //   两路en信号是以备万一某些指令只有op确定而funct任意，可以不判断funct
  //   op_std, funct_std用常量
  //   （例如I型和J型指令，funct对应的位数都是立即数，没意义）
endmodule

module big_andgate_32 (
  input  in_1,
  input  in_2,
  input  in_3,
  input  in_4,
  input  in_5,
  input  in_6,
  input  in_7,
  input  in_8,
  input  in_9,
  input  in_10,
  input  in_11,
  input  in_12,
  input  in_13,
  input  in_14,
  input  in_15,
  input  in_16,
  input  in_17,
  input  in_18,
  input  in_19,
  input  in_20,
  input  in_21,
  input  in_22,
  input  in_23,
  input  in_24,
  input  in_25,
  input  in_26,
  input  in_27,
  input  in_28,
  input  in_29,
  input  in_30,
  input  in_31,
  input  in_32,
  output out_33
);

  Pull_Resistor pull_resistor_1 (.node(in_1));
  Pull_Resistor pull_resistor_2 (.node(in_9));
  Pull_Resistor pull_resistor_3 (.node(in_17));
  Pull_Resistor pull_resistor_4 (.node(in_25));
  Pull_Resistor pull_resistor_5 (.node(in_2));
  Pull_Resistor pull_resistor_6 (.node(in_10));
  Pull_Resistor pull_resistor_7 (.node(in_18));
  Pull_Resistor pull_resistor_8 (.node(in_26));
  Pull_Resistor pull_resistor_9 (.node(in_3));
  Pull_Resistor pull_resistor_10 (.node(in_11));
  Pull_Resistor pull_resistor_11 (.node(in_19));
  Pull_Resistor pull_resistor_12 (.node(in_27));
  Pull_Resistor pull_resistor_13 (.node(in_4));
  Pull_Resistor pull_resistor_14 (.node(in_12));
  Pull_Resistor pull_resistor_15 (.node(in_20));
  Pull_Resistor pull_resistor_16 (.node(in_28));
  Pull_Resistor pull_resistor_17 (.node(in_6));
  Pull_Resistor pull_resistor_18 (.node(in_5));
  Pull_Resistor pull_resistor_19 (.node(in_14));
  Pull_Resistor pull_resistor_20 (.node(in_13));
  Pull_Resistor pull_resistor_21 (.node(in_21));
  Pull_Resistor pull_resistor_22 (.node(in_22));
  Pull_Resistor pull_resistor_23 (.node(in_30));
  Pull_Resistor pull_resistor_24 (.node(in_29));
  Pull_Resistor pull_resistor_25 (.node(in_7));
  Pull_Resistor pull_resistor_26 (.node(in_15));
  Pull_Resistor pull_resistor_27 (.node(in_23));
  Pull_Resistor pull_resistor_28 (.node(in_31));
  Pull_Resistor pull_resistor_29 (.node(in_8));
  Pull_Resistor pull_resistor_30 (.node(in_16));
  Pull_Resistor pull_resistor_31 (.node(in_24));
  Pull_Resistor pull_resistor_32 (.node(in_32));
  and and_1 (out_33, in_1, in_2, in_3, in_4, in_5, in_6, in_7, in_8, in_9, in_10, in_11, in_12, in_13, in_14, in_15, in_16, in_17, in_18, in_19, in_20, in_21, in_22, in_23, in_24, in_25, in_26, in_27, in_28, in_29, in_30, in_31, in_32);

  // Notes on the sheet:
  //   在控制单元这里定制的专用与门，自带32路1位输入，所有的X输入自动下拉为0，不影响有输入的端。全X则输出0
endmodule

module big_orgate_32 (
  input  in_1,
  input  in_2,
  input  in_3,
  input  in_4,
  input  in_5,
  input  in_6,
  input  in_7,
  input  in_8,
  input  in_9,
  input  in_10,
  input  in_11,
  input  in_12,
  input  in_13,
  input  in_14,
  input  in_15,
  input  in_16,
  input  in_17,
  input  in_18,
  input  in_19,
  input  in_20,
  input  in_21,
  input  in_22,
  input  in_23,
  input  in_24,
  input  in_25,
  input  in_26,
  input  in_27,
  input  in_28,
  input  in_29,
  input  in_30,
  input  in_31,
  input  in_32,
  output out_33
);

  Pull_Resistor pull_resistor_1 (.node(in_1));
  Pull_Resistor pull_resistor_2 (.node(in_9));
  Pull_Resistor pull_resistor_3 (.node(in_17));
  Pull_Resistor pull_resistor_4 (.node(in_25));
  Pull_Resistor pull_resistor_5 (.node(in_2));
  Pull_Resistor pull_resistor_6 (.node(in_10));
  Pull_Resistor pull_resistor_7 (.node(in_18));
  Pull_Resistor pull_resistor_8 (.node(in_26));
  Pull_Resistor pull_resistor_9 (.node(in_3));
  Pull_Resistor pull_resistor_10 (.node(in_11));
  Pull_Resistor pull_resistor_11 (.node(in_19));
  Pull_Resistor pull_resistor_12 (.node(in_27));
  Pull_Resistor pull_resistor_13 (.node(in_4));
  Pull_Resistor pull_resistor_14 (.node(in_12));
  Pull_Resistor pull_resistor_15 (.node(in_20));
  Pull_Resistor pull_resistor_16 (.node(in_28));
  Pull_Resistor pull_resistor_17 (.node(in_5));
  Pull_Resistor pull_resistor_18 (.node(in_6));
  Pull_Resistor pull_resistor_19 (.node(in_13));
  Pull_Resistor pull_resistor_20 (.node(in_14));
  Pull_Resistor pull_resistor_21 (.node(in_22));
  Pull_Resistor pull_resistor_22 (.node(in_21));
  Pull_Resistor pull_resistor_23 (.node(in_29));
  Pull_Resistor pull_resistor_24 (.node(in_30));
  Pull_Resistor pull_resistor_25 (.node(in_7));
  Pull_Resistor pull_resistor_26 (.node(in_15));
  Pull_Resistor pull_resistor_27 (.node(in_23));
  Pull_Resistor pull_resistor_28 (.node(in_31));
  Pull_Resistor pull_resistor_29 (.node(in_8));
  Pull_Resistor pull_resistor_30 (.node(in_16));
  Pull_Resistor pull_resistor_31 (.node(in_24));
  Pull_Resistor pull_resistor_32 (.node(in_32));
  or or_1 (out_33, in_1, in_2, in_3, in_4, in_5, in_6, in_7, in_8, in_9, in_10, in_11, in_12, in_13, in_14, in_15, in_16, in_17, in_18, in_19, in_20, in_21, in_22, in_23, in_24, in_25, in_26, in_27, in_28, in_29, in_30, in_31, in_32);

  // Notes on the sheet:
  //   在控制单元这里定制的专用或门，自带32路1位输入，所有的X输入自动下拉为0，不影响有输入的端。全X则输出0
endmodule

module andgate_8 (
  input  In0,
  input  In1,
  input  In2,
  input  In3,
  input  In4,
  input  In5,
  input  In6,
  input  In7,
  output out
);

  Pull_Resistor pull_resistor_1 (.node(In1));
  Pull_Resistor pull_resistor_2 (.node(In0));
  Pull_Resistor pull_resistor_3 (.node(In5));
  Pull_Resistor pull_resistor_4 (.node(In2));
  Pull_Resistor pull_resistor_5 (.node(In3));
  Pull_Resistor pull_resistor_6 (.node(In4));
  Pull_Resistor pull_resistor_7 (.node(In7));
  Pull_Resistor pull_resistor_8 (.node(In6));
  and and_1 (out, In0, In1, In2, In3, In4, In5, In6, In7);
endmodule

module orgate_8 (
  input  In0,
  input  In1,
  input  In2,
  input  In3,
  input  In4,
  input  In5,
  input  In6,
  input  In7,
  output out
);

  Pull_Resistor pull_resistor_1 (.node(In1));
  Pull_Resistor pull_resistor_2 (.node(In0));
  Pull_Resistor pull_resistor_3 (.node(In4));
  Pull_Resistor pull_resistor_4 (.node(In3));
  Pull_Resistor pull_resistor_5 (.node(In2));
  Pull_Resistor pull_resistor_6 (.node(In5));
  Pull_Resistor pull_resistor_7 (.node(In7));
  Pull_Resistor pull_resistor_8 (.node(In6));
  or or_1 (out, In0, In1, In2, In3, In4, In5, In6, In7);
endmodule
