// Logisim project Control_old.circ as structural Verilog: 6 circuits, main circuit Control
module Control (
  input  [5:0] opcode,
  input  [5:0] funct,
  output MemtoReg,
  output MemWrite,
  output [3:0] ALUop,
  output EXTop,
  output ALUsrc,
  output [1:0] RegDst,
  output RegWrite,
  output [3:0] Branch,
  output Jump,
  output JmpSrc,
  output JmpLnk
);

  wire add, addi, addu, beq, j, jal, jalr, jr, lb, lbu, lh, lhu, loadstore, lui, lw, nop, or_4_out, or_6_out,
       or_7_out, or_8_out, or_9_out, or_10_out, or_11_out, or_12_out, ori, sb, sh, sub, subu, sw, typeI,
       typeJ, typeR;
  wire [1:0] multiplexer_1_out, multiplexer_2_out;
  wire [2:0] multiplexer_8_out, multiplexer_9_out, NPCop;
  wire [3:0] multiplexer_3_out, multiplexer_4_out, multiplexer_5_out, multiplexer_6_out;

  or or_1 (typeJ, j, jal);
  instr_judger instr_judger_1 (
    .op(opcode), .op_std({6{1'b0}}), .op_en(1'b1), .funct(funct), .funct_std(6'b100000), .funct_en(1'b1),
    .correct(add));
  instr_judger instr_judger_2 (
    .op(opcode), .op_std({6{1'b0}}), .op_en(1'b1), .funct(funct), .funct_std(6'b100010), .funct_en(1'b1),
    .correct(sub));
  instr_judger instr_judger_3 (
    .op(opcode), .op_std({6{1'b0}}), .op_en(1'b1), .funct(funct), .funct_std(6'b100001), .funct_en(1'b1),
    .correct(addu));
  instr_judger instr_judger_4 (
    .op(opcode), .op_std({6{1'b0}}), .op_en(1'b1), .funct(funct), .funct_std(6'b100011), .funct_en(1'b1),
    .correct(subu));
  instr_judger instr_judger_5 (
    .op(opcode), .op_std({6{1'b0}}), .op_en(1'b1), .funct(funct), .funct_std(6'b001001), .funct_en(1'b1),
    .correct(jalr));
  instr_judger instr_judger_6 (
    .op(opcode), .op_std({6{1'b0}}), .op_en(1'b1), .funct(funct), .funct_std(6'b001000), .funct_en(1'b1),
    .correct(jr));
  or or_2 (typeR, add, sub, addu, subu, nop);
  instr_judger instr_judger_7 (
    .op(opcode), .op_std({6{1'b0}}), .op_en(1'b1), .funct(funct), .funct_std({6{1'b0}}), .funct_en(1'b1),
    .correct(nop));
  instr_judger instr_judger_8 (
    .op(opcode), .op_std(6'b001000), .op_en(1'b1), .funct(funct), .funct_std({6{1'b0}}), .funct_en(1'b0),
    .correct(addi));
  instr_judger instr_judger_9 (
    .op(opcode), .op_std(6'b101011), .op_en(1'b1), .funct(funct), .funct_std({6{1'b0}}), .funct_en(1'b0),
    .correct(sw));
  instr_judger instr_judger_10 (
    .op(opcode), .op_std(6'b100011), .op_en(1'b1), .funct(funct), .funct_std({6{1'b0}}), .funct_en(1'b0),
    .correct(lw));
  instr_judger instr_judger_11 (
    .op(opcode), .op_std(6'b001111), .op_en(1'b1), .funct(funct), .funct_std({6{1'b0}}), .funct_en(1'b0),
    .correct(lui));
  instr_judger instr_judger_12 (
    .op(opcode), .op_std(6'b001101), .op_en(1'b1), .funct(funct), .funct_std({6{1'b0}}), .funct_en(1'b0),
    .correct(ori));
  instr_judger instr_judger_13 (
    .op(opcode), .op_std(6'b101000), .op_en(1'b1), .funct(funct), .funct_std({6{1'b0}}), .funct_en(1'b0),
    .correct(sb));
  instr_judger instr_judger_14 (
    .op(opcode), .op_std(6'b101001), .op_en(1'b1), .funct(funct), .funct_std({6{1'b0}}), .funct_en(1'b0),
    .correct(sh));
  instr_judger instr_judger_15 (
    .op(opcode), .op_std(6'b100000), .op_en(1'b1), .funct(funct), .funct_std({6{1'b0}}), .funct_en(1'b0),
    .correct(lb));
  instr_judger instr_judger_16 (
    .op(opcode), .op_std(6'b100001), .op_en(1'b1), .funct(funct), .funct_std({6{1'b0}}), .funct_en(1'b0),
    .correct(lh));
  instr_judger instr_judger_17 (
    .op(opcode), .op_std(6'b100100), .op_en(1'b1), .funct(funct), .funct_std({6{1'b0}}), .funct_en(1'b0),
    .correct(lbu));
  instr_judger instr_judger_18 (
    .op(opcode), .op_std(6'b100101), .op_en(1'b1), .funct(funct), .funct_std({6{1'b0}}), .funct_en(1'b0),
    .correct(lhu));
  instr_judger instr_judger_19 (
    .op(opcode), .op_std(6'b000100), .op_en(1'b1), .funct(funct), .funct_std({6{1'b0}}), .funct_en(1'b0),
    .correct(beq));
  or or_3 (typeI, addi, lw, sw, lui, ori, sb, sh, lb, lh, lbu, lhu, beq);
  instr_judger instr_judger_20 (
    .op(opcode), .op_std(6'b000010), .op_en(1'b1), .funct(funct), .funct_std({6{1'b0}}), .funct_en(1'b0),
    .correct(j));
  instr_judger instr_judger_21 (
    .op(opcode), .op_std(6'b000011), .op_en(1'b1), .funct(funct), .funct_std({6{1'b0}}), .funct_en(1'b0),
    .correct(jal));
  or or_4 (or_4_out, addi, add, addu);
  or or_5 (loadstore, lw, sw, sb, sh, lb, lh, lbu, lhu);
  or or_6 (or_6_out, or_4_out, loadstore);
  or or_7 (or_7_out, sub, subu);
  or or_8 (or_8_out, or_7_out, or_9_out);
  or or_9 (or_9_out, beq, 1'b0);
  or or_10 (or_10_out, beq, 1'b0);
  or or_11 (or_11_out, j, jal);
  or or_12 (or_12_out, addi, lui, ori, 1'b0, 1'b0);
  Multiplexer #(.width(2), .disabled(0), .enable("false")) multiplexer_1 (
    .in0(2'b00), .in1(2'b01), .out(multiplexer_1_out), .sel(typeI));
  Multiplexer #(.width(2), .disabled(0), .enable("false")) multiplexer_2 (
    .in0(2'b00), .in1(2'b10), .out(multiplexer_2_out), .sel(jal));
  Multiplexer #(.width(4), .disabled(0), .enable("false")) multiplexer_3 (
    .in0(4'b0000), .in1(4'b0010), .out(multiplexer_3_out), .sel(or_6_out));
  Multiplexer #(.width(4), .disabled(0), .enable("false")) multiplexer_4 (
    .in0(4'b0000), .in1(4'b0011), .out(multiplexer_4_out), .sel(or_8_out));
  Multiplexer #(.width(4), .disabled(0), .enable("false")) multiplexer_5 (
    .in0(4'b0000), .in1(4'b0001), .out(multiplexer_5_out), .sel(ori));
  Multiplexer #(.width(4), .disabled(0), .enable("false")) multiplexer_6 (
    .in0(4'b0000), .in1(4'b1010), .out(multiplexer_6_out), .sel(lui));
  Multiplexer #(.width(4), .disabled(0), .enable("false")) multiplexer_7 (
    .in0(4'b0000), .in1(4'b0001), .out(Branch), .sel(beq));
  Multiplexer #(.width(3), .disabled(0), .enable("false")) multiplexer_8 (
    .in0(3'b000), .in1(3'b001), .out(multiplexer_8_out), .sel(or_10_out));
  assign NPCop = multiplexer_8_out | multiplexer_9_out;  // OR_Gate or_13, 3 bits wide
  Multiplexer #(.width(3), .disabled(0), .enable("false")) multiplexer_9 (
    .in0(3'b000), .in1(3'b010), .out(multiplexer_9_out), .sel(or_11_out));
  or or_14 (MemWrite, sh, sw, sb);
  nor nor_1 (RegWrite, beq, nop, j, sh, sw, sb);
  or or_15 (MemtoReg, lw, lb, lh, lbu, lhu);
  or or_16 (ALUsrc, loadstore, or_12_out);
  assign RegDst = multiplexer_1_out | multiplexer_2_out;  // OR_Gate or_17, 2 bits wide
  nor nor_2 (EXTop, ori, 1'b0);
  or or_18 (Jump, j, jal, jalr, jr);
  or or_19 (JmpSrc, j, jal);
  or or_20 (JmpLnk, jal, jalr);
  assign ALUop = multiplexer_3_out | multiplexer_4_out | multiplexer_5_out | multiplexer_6_out;  // OR_Gate or_21, 4 bits wide

  // Notes on the sheet:
  //   Control Unit: CPU的控制器单元
  //   加指令方法：复制一个instr模块，修改opcode和funct的常量以及输出的标签即可
  //   R-type
  //   I-type
  //   TODO: 重构一下！！！！！！！！！！！
  //   J-type
endmodule

module instr_judger (
  input  [5:0] op,
  input  [5:0] op_std,
  input  op_en,
  input  [5:0] funct,
  input  [5:0] funct_std,
  input  funct_en,
  output correct
);

  wire nor_1_out, nor_2_out, or_1_out, or_2_out;
  wire [5:0] xor_1_out, xor_2_out;

  assign xor_1_out = op ^ op_std;  // XOR_Gate xor_1, 6 bits wide
  assign xor_2_out = funct ^ funct_std;  // XOR_Gate xor_2, 6 bits wide
  nor nor_1 (nor_1_out, xor_1_out[0], xor_1_out[1], xor_1_out[2], xor_1_out[3], xor_1_out[4], xor_1_out[5]);
  nor nor_2 (nor_2_out, xor_2_out[0], xor_2_out[1], xor_2_out[2], xor_2_out[3], xor_2_out[4], xor_2_out[5]);
  or or_1 (or_1_out, nor_1_out, ~op_en);  // OR_Gate
  or or_2 (or_2_out, nor_2_out, ~funct_en);  // OR_Gate
  and and_1 (correct, or_1_out, or_2_out);

  // Notes on the sheet:
  //   指令判断器：根据给定的opcode和funct判断一条指令是不是某指令
  //   op: 输入指令的op，op_std: 要判断是不是的指令的op，op_en: 是否检查op一致
  //   输出：是否为某指令
  //   例如：将op_std设定为0，funct_std设定为100000，若输入的op和funct一致则该指令为add指令
  //   下面的funct同理
  //   使用方法：op以及funct连接模块输入的op和funct
  //   两路en信号是以备万一某些指令只有op确定而funct任意，可以不判断funct
  //   op_std, funct_std用常量
  //   （例如I型和J型指令，funct对应的位数都是立即数，没意义）
endmodule

module big_andgate_32 (
  input  in_1,
  input  in_2,
  input  in_3,
  input  in_4,
  input  in_5,
  input  in_6,
  input  in_7,
  input  in_8,
  input  in_9,
  input  in_10,
  input  in_11,
  input  in_12,
  input  in_13,
  input  in_14,
  input  in_15,
  input  in_16,
  input  in_17,
  input  in_18,
  input  in_19,
  input  in_20,
  input  in_21,
  input  in_22,
  input  in_23,
  input  in_24,
  input  in_25,
  input  in_26,
  input  in_27,
  input  in_28,
  input  in_29,
  input  in_30,
  input  in_31,
  input  in_32,
  output out_33
);

  Pull_Resistor pull_resistor_1 (.node(in_1));
  Pull_Resistor pull_resistor_2 (.node(in_9));
  Pull_Resistor pull_resistor_3 (.node(in_17));
  Pull_Resistor pull_resistor_4 (.node(in_25));
  Pull_Resistor pull_resistor_5 (.node(in_2));
  Pull_Resistor pull_resistor_6 (.node(in_10));
  Pull_Resistor pull_resistor_7 (.node(in_18));
  Pull_Resistor pull_resistor_8 (.node(in_26));
  Pull_Resistor pull_resistor_9 (.node(in_3));
  Pull_Resistor pull_resistor_10 (.node(in_11));
  Pull_Resistor pull_resistor_11 (.node(in_19));
  Pull_Resistor pull_resistor_12 (.node(in_27));
  Pull_Resistor pull_resistor_13 (.node(in_4));
  Pull_Resistor pull_resistor_14 (.node(in_12));
  Pull_Resistor pull_resistor_15 (.node(in_20));
  Pull_Resistor pull_resistor_16 (.node(in_28));
  Pull_Resistor pull_resistor_17 (.node(in_5));
  Pull_Resistor pull_resistor_18 (.node(in_6));
  Pull_Resistor pull_resistor_19 (.node(in_14));
  Pull_Resistor pull_resistor_20 (.node(in_13));
  Pull_Resistor pull_resistor_21 (.node(in_22));
  Pull_Resistor pull_resistor_22 (.node(in_21));
  Pull_Resistor pull_resistor_23 (.node(in_29));
  Pull_Resistor pull_resistor_24 (.node(in_30));
  Pull_Resistor pull_resistor_25 (.node(in_7));
  Pull_Resistor pull_resistor_26 (.node(in_15));
  Pull_Resistor pull_resistor_27 (.node(in_23));
  Pull_Resistor pull_resistor_28 (.node(in_31));
  Pull_Resistor pull_resistor_29 (.node(in_8));
  Pull_Resistor pull_resistor_30 (.node(in_16));
  Pull_Resistor pull_resistor_31 (.node(in_24));
  Pull_Resistor pull_resistor_32 (.node(in_32));
  and and_1 (out_33, in_1, in_2, in_3, in_4, in_5, in_6, in_7, in_8, in_9, in_10, in_11, in_12, in_13, in_14, in_15, in_16, in_17, in_18, in_19, in_20, in_21, in_22, in_23, in_24, in_25, in_26, in_27, in_28, in_29, in_30, in_31, in_32);

  // Notes on the sheet:
  //   在控制单元这里定制的专用与门，自带32路1位输入，所有的X输入自动下拉为0，不影响有输入的端。全X则输出0
endmodule

module big_orgate_32 (
  input  in_1,
  input  in_2,
  input  in_3,
  input  in_4,
  input  in_5,
  input  in_6,
  input  in_7,
  input  in_8,
  input  in_9,
  input  in_10,
  input  in_11,
  input  in_12,
  input  in_13,
  input  in_14,
  input  in_15,
  input  in_16,
  input  in_17,
  input  in_18,
  input  in_19,
  input  in_20,
  input  in_21,
  input  in_22,
  input  in_23,
  input  in_24,
  input  in_25,
  input  in_26,
  input  in_27,
  input  in_28,
  input  in_29,
  input  in_30,
  input  in_31,
  input  in_32,
  output out_33
);

  Pull_Resistor pull_resistor_1 (.node(in_1));
  Pull_Resistor pull_resistor_2 (.node(in_9));
  Pull_Resistor pull_resistor_3 (.node(in_17));
  Pull_Resistor pull_resistor_4 (.node(in_25));
  Pull_Resistor pull_resistor_5 (.node(in_2));
  Pull_Resistor pull_resistor_6 (.node(in_10));
  Pull_Resistor pull_resistor_7 (.node(in_18));
  Pull_Resistor pull_resistor_8 (.node(in_26));
  Pull_Resistor pull_resistor_9 (.node(in_3));
  Pull_Resistor pull_resistor_10 (.node(in_11));
  Pull_Resistor pull_resistor_11 (.node(in_19));
  Pull_Resistor pull_resistor_12 (.node(in_27));
  Pull_Resistor pull_resistor_13 (.node(in_4));
  Pull_Resistor pull_resistor_14 (.node(in_12));
  Pull_Resistor pull_resistor_15 (.node(in_20));
  Pull_Resistor pull_resistor_16 (.node(in_28));
  Pull_Resistor pull_resistor_17 (.node(in_6));
  Pull_Resistor pull_resistor_18 (.node(in_5));
  Pull_Resistor pull_resistor_19 (.node(in_14));
  Pull_Resistor pull_resistor_20 (.node(in_13));
  Pull_Resistor pull_resistor_21 (.node(in_22));
  Pull_Resistor pull_resistor_22 (.node(in_21));
  Pull_Resistor pull_resistor_23 (.node(in_30));
  Pull_Resistor pull_resistor_24 (.node(in_29));
  Pull_Resistor pull_resistor_25 (.node(in_7));
  Pull_Resistor pull_resistor_26 (.node(in_15));
  Pull_Resistor pull_resistor_27 (.node(in_23));
  Pull_Resistor pull_resistor_28 (.node(in_31));
  Pull_Resistor pull_resistor_29 (.node(in_8));
  Pull_Resistor pull_resistor_30 (.node(in_16));
  Pull_Resistor pull_resistor_31 (.node(in_24));
  Pull_Resistor pull_resistor_32 (.node(in_32));
  or or_1 (out_33, in_1, in_2, in_3, in_4, in_5, in_6, in_7, in_8, in_9, in_10, in_11, in_12, in_13, in_14, in_15, in_16, in_17, in_18, in_19, in_20, in_21, in_22, in_23, in_24, in_25, in_26, in_27, in_28, in_29, in_30, in_31, in_32);

  // Notes on the sheet:
  //   在控制单元这里定制的专用或门，自带32路1位输入，所有的X输入自动下拉为0，不影响有输入的端。全X则输出0
endmodule

module andgate_8 (
  input  In0,
  input  In1,
  input  In2,
  input  In3,
  input  In4,
  input  In5,
  input  In6,
  input  In7,
  output out
);

  Pull_Resistor pull_resistor_1 (.node(In0));
  Pull_Resistor pull_resistor_2 (.node(In1));
  Pull_Resistor pull_resistor_3 (.node(In2));
  Pull_Resistor pull_resistor_4 (.node(In4));
  Pull_Resistor pull_resistor_5 (.node(In5));
  Pull_Resistor pull_resistor_6 (.node(In3));
  Pull_Resistor pull_resistor_7 (.node(In6));
  Pull_Resistor pull_resistor_8 (.node(In7));
  and and_1 (out, In0, In1, In2, In3, In4, In5, In6, In7);
endmodule

module orgate_8 (
  input  In0,
  input  In1,
  input  In2,
  input  In3,
  input  In4,
  input  In5,
  input  In6,
  input  In7,
  output out
);

  Pull_Resistor pull_resistor_1 (.node(In0));
  Pull_Resistor pull_resistor_2 (.node(In1));
  Pull_Resistor pull_resistor_3 (.node(In2));
  Pull_Resistor pull_resistor_4 (.node(In4));
  Pull_Resistor pull_resistor_5 (.node(In5));
  Pull_Resistor pull_resistor_6 (.node(In3));
  Pull_Resistor pull_resistor_7 (.node(In7));
  Pull_Resistor pull_resistor_8 (.node(In6));
  and and_1 (out, In0, In1, In2, In3, In4, In5, In6, In7);
endmodule
