// Logisim project DM.circ as structural Verilog: 3 circuits, main circuit DM
module DM (
  input  clk,
  input  rst,
  input  WE,
  input  [1:0] size,
  input  extop,
  input  [31:0] A,
  input  [31:0] WD,
  output [31:0] RD
);

  wire decoder_1_out0, decoder_1_out1, decoder_1_out2, decoder_1_out3, decoder_2_out0, decoder_2_out1,
       offset_half;
  wire [1:0] offset_byte;
  wire [7:0] multiplexer_6_out, sb;
  wire [15:0] multiplexer_5_out, sh;
  wire [23:0] Addr;
  wire [31:0] bit_extender_3_out, bit_extender_4_out, bit_extender_5_out, bit_extender_6_out, \byte , half,
       MemWord, sbToMem, shToMem, WordToMem;

  // Probe on A
  // Probe on WD
  Decoder #(.select(2), .disabled(0), .enable("false")) decoder_1 (
    .out0(decoder_1_out0), .out1(decoder_1_out1), .out2(decoder_1_out2), .out3(decoder_1_out3),
    .sel(offset_byte));
  dm_addr dm_addr_1 (.Addr32(A), .Addr24(Addr), .offset_byte(offset_byte), .offset_half(offset_half));
  Bit_Extender #(.in_width(32)) bit_extender_1 (.in(WD), .out(sh));
  Bit_Extender #(.in_width(32), .out_width(8)) bit_extender_2 (.in(WD), .out(sb));
  Multiplexer #(.width(8), .disabled(0), .enable("false")) multiplexer_1 (
    .in0(MemWord[7:0]), .in1(sb), .out(sbToMem[7:0]), .sel(decoder_1_out0));
  Multiplexer #(.width(8), .disabled(0), .enable("false")) multiplexer_2 (
    .in0(MemWord[23:16]), .in1(sb), .out(sbToMem[23:16]), .sel(decoder_1_out2));
  Pull_Resistor pull_resistor_1 (.node(size));
  Multiplexer #(.width(8), .disabled(0), .enable("false")) multiplexer_3 (
    .in0(MemWord[15:8]), .in1(sb), .out(sbToMem[15:8]), .sel(decoder_1_out1));
  Multiplexer #(.width(8), .disabled(0), .enable("false")) multiplexer_4 (
    .in0(MemWord[31:24]), .in1(sb), .out(sbToMem[31:24]), .sel(decoder_1_out3));
  Pull_Resistor pull_resistor_2 (.node(extop));
  RAM #(.addrWidth(24), .dataWidth(32), .bus("separate")) ram_1 (
    .addr(Addr), .din(WordToMem), .data(MemWord), .str(WE), .sel(1'b1), .clk(clk), .ld(1'b1), .clr(rst));
  Multiplexer #(.width(16), .disabled(0), .enable("false")) multiplexer_5 (
    .in0(MemWord[15:0]), .in1(MemWord[31:16]), .out(multiplexer_5_out), .sel(offset_half));
  Multiplexer #(.select(2), .width(8), .disabled(0), .enable("false")) multiplexer_6 (
    .in0(MemWord[7:0]), .in1(MemWord[15:8]), .in2(MemWord[23:16]), .in3(MemWord[31:24]),
    .out(multiplexer_6_out), .sel(offset_byte));
  assign bit_extender_3_out = {{16{1'b0}}, multiplexer_5_out};  // Bit_Extender bit_extender_3
  Multiplexer #(.width(32), .disabled(0), .enable("false")) multiplexer_7 (
    .in0(bit_extender_3_out), .in1(bit_extender_4_out), .out(half), .sel(extop));
  assign bit_extender_4_out = {{16{multiplexer_5_out[15]}}, multiplexer_5_out};  // Bit_Extender bit_extender_4
  assign bit_extender_5_out = {{24{1'b0}}, multiplexer_6_out};  // Bit_Extender bit_extender_5
  Multiplexer #(.width(32), .disabled(0), .enable("false")) multiplexer_8 (
    .in0(bit_extender_5_out), .in1(bit_extender_6_out), .out(\byte ), .sel(extop));
  assign bit_extender_6_out = {{24{multiplexer_6_out[7]}}, multiplexer_6_out};  // Bit_Extender bit_extender_6
  Multiplexer #(.select(2), .width(32), .disabled(0), .enable("false")) multiplexer_9 (
    .in0(WD), .in1(shToMem), .in2(sbToMem), .out(WordToMem), .sel(size));  // open: in3
  Decoder #(.disabled(0), .enable("false")) decoder_2 (.out0(decoder_2_out0), .out1(decoder_2_out1), .sel(offset_half));
  Multiplexer #(.width(16), .disabled(0), .enable("false")) multiplexer_10 (
    .in0(MemWord[15:0]), .in1(sh), .out(shToMem[15:0]), .sel(decoder_2_out0));
  Multiplexer #(.width(16), .disabled(0), .enable("false")) multiplexer_11 (
    .in0(MemWord[31:16]), .in1(sh), .out(shToMem[31:16]), .sel(decoder_2_out1));
  Multiplexer #(.select(2), .width(32), .disabled(0), .enable("false")) multiplexer_12 (
    .in0(MemWord), .in1(half), .in2(\byte ), .out(RD), .sel(size));  // open: in3

  // Notes on the sheet:
  //   Data Memory 数据存储器
  //   clk:时钟，rst:异步重置
  //   A: 地址，WD: 要写入的数据
  //   WE: 写使能(1可写0不写)
  //   size: 读写的大小规模(00字，01半字，10字节，11留空)
  //   extop: 符号扩展类型(1有符号0无符号)，仅在读半字和字节时有效
endmodule

module dm_addr (
  input  [31:0] Addr32,
  output [23:0] Addr24,
  output [1:0] offset_byte,
  output offset_half
);

  wire [31:0] shifter_1_out;

  Shifter #(.width(32), .shift("lr")) shifter_1 (.in(Addr32), .\dist (5'b00010), .out(shifter_1_out));
  Bit_Extender #(.in_width(32), .out_width(24)) bit_extender_1 (.in(shifter_1_out), .out(Addr24));

  assign offset_byte = Addr32[1:0];
  assign offset_half = Addr32[1];

  // Notes on the sheet:
  //   dm_addr: 将DM的32位输入地址转化成24位的RAM地址
endmodule

module test (
  input  [31:0] in_1,
  input  in_2,
  input  in_3,
  input  [1:0] in_4,
  input  [31:0] in_5,
  input  in_6
);

  wire clock_1_out;
  wire [31:0] dm_1_rd;

  // Probe on in_1
  // Probe on in_5
  DM dm_1 (.A(in_1), .WD(in_5), .RD(dm_1_rd), .clk(clock_1_out), .rst(in_6), .WE(in_2), .extop(in_3), .size(in_4));
  Clock clock_1 (.out(clock_1_out));
  // Probe on dm_1_rd
endmodule
