// Logisim project EXT.circ as structural Verilog: 1 circuit, main circuit EXT
module EXT (
  input  [15:0] in,
  input  EXTop,
  output [31:0] out
);

  wire [31:0] bit_extender_1_out, bit_extender_2_out;

  assign bit_extender_1_out = {{16{1'b0}}, in};  // Bit_Extender bit_extender_1
  assign bit_extender_2_out = {{16{in[15]}}, in};  // Bit_Extender bit_extender_2
  Multiplexer #(.width(32), .disabled(0), .enable("false")) multiplexer_1 (
    .in0(bit_extender_1_out), .in1(bit_extender_2_out), .out(out), .sel(EXTop));
endmodule
