// Logisim project IF.circ as structural Verilog: 1 circuit, main circuit IF
module IF (
  input  [31:0] Instr,
  output [5:0] op,
  output [4:0] rs,
  output [4:0] rt,
  output [4:0] rd,
  output [4:0] shamt,
  output [5:0] funct,
  output [15:0] imm,
  output [25:0] addr
);


  assign addr = Instr[25:0];
  assign funct = Instr[5:0];
  assign imm = Instr[15:0];
  assign op = Instr[31:26];
  assign rd = Instr[15:11];
  assign rs = Instr[25:21];
  assign rt = Instr[20:16];
  assign shamt = Instr[10:6];

  // Notes on the sheet:
  //   Instruction Fetch(IF)模块：将指令的每个部分拆分出来
  //   将32位的指令按照R,I,J型指令将每个部分拆分出来
  //   R-type
  //   I-type
  //   J-type
endmodule
