// Logisim project IM.circ as structural Verilog: 2 circuits, main circuit IM
module IM (
  input  [31:0] A,
  output [31:0] RD
);

  wire [23:0] im_addr_1_addr24;

  // Probe on A
  im_addr im_addr_1 (.Addr32(A), .Addr24(im_addr_1_addr24));
  ROM #(.addrWidth(24), .dataWidth(32)) rom_1 (.addr(im_addr_1_addr24), .data(RD), .sel(1'b1));
  // Probe on RD

  // Notes on the sheet:
  //   Instruction Memory 指令存储器
  //   im_addr模块将32位的PC转化成24位的ROM地址
  //   若PC有其他要求(例如从0x00003000开始，则修改此模块)
endmodule

module im_addr (
  input  [31:0] Addr32,
  output [23:0] Addr24
);

  wire [31:0] shifter_1_out, subtractor_1_out;

  Subtractor #(.width(32)) subtractor_1 (.a(Addr32), .b(32'h3000), .out(subtractor_1_out));  // open: bin, bout
  Shifter #(.width(32), .shift("lr")) shifter_1 (.in(subtractor_1_out), .\dist (5'b00010), .out(shifter_1_out));
  Bit_Extender #(.in_width(32), .out_width(24)) bit_extender_1 (.in(shifter_1_out), .out(Addr24));

  // Notes on the sheet:
  //   im_addr: 将32位的地址转化为24位的适合ROM的地址
  //   注：若PC地址从0x00003000开始，则修改该模块！！！！
endmodule
