// Logisim project NPC.circ as structural Verilog: 1 circuit, main circuit NPC
module NPC (
  input  [31:0] PC,
  input  [15:0] imm16,
  input  [25:0] addr26,
  input  [31:0] ra32,
  input  [2:0] op,
  output [31:0] nextPC,
  output [31:0] PC4
);

  wire [31:0] bit_extender_1_out, branch, imm;

  assign bit_extender_1_out = {{16{imm16[15]}}, imm16};  // Bit_Extender bit_extender_1
  Shifter #(.width(32)) shifter_1 (.in(bit_extender_1_out), .\dist (5'b00010), .out(imm));
  Adder #(.width(32)) adder_1 (.a(PC), .b(32'h4), .out(PC4));  // open: cin, cout
  Adder #(.width(32)) adder_2 (.a(PC4), .b(imm), .out(branch));  // open: cin, cout
  Multiplexer #(.select(3), .width(32), .disabled(0), .enable("false")) multiplexer_1 (
    .in0(PC4), .in1(branch), .in2({PC[31:28], addr26, 2'b00}), .in3(ra32), .out(nextPC), .sel(op));  // open: in4, in5, in6, in7

  // Other names for the same wires on the sheet: addr[31:2] = {PC[31:28], addr26}; ra[31:0] = ra32

  // Notes on the sheet:
  //   NPC模块:Next PC，计算下一路PC的值
endmodule
