// Logisim project PC.circ as structural Verilog: 1 circuit, main circuit PC
module PC (
  input  clk,
  input  rst,
  input  [31:0] nextPC,
  output [31:0] PC
);

  wire init;
  wire [31:0] PC_q;

  Counter #(.width(1), .max('h1), .ongoal("stay")) initcnt (
    .carry(init), .clk(clk), .clr(rst));  // open: load, D, count, Q
  Register #(.width(32)) u_PC (.D(nextPC), .Q(PC_q), .clk(clk), .clr(rst));  // open: en
  Multiplexer #(.width(32), .disabled(0), .enable("false")) multiplexer_1 (
    .in0(32'h3000), .in1(PC_q), .out(PC), .sel(init));

  // Notes on the sheet:
  //   Program Counter: 指令计数器
  //   如果PC的初始值是0x00003000则修改MUX处的常量
endmodule
