// Logisim project Shifter.circ as structural Verilog: 6 circuits, main circuit Shifter
module Shifter (
  input  [31:0] In,
  input  [4:0] sh,
  input  [2:0] op,
  output [31:0] Out
);

  wire [31:0] aright, lleft, lright, rleft, rright;

  logicalleft logicalleft_1 (.In(In), .sh(sh), .Out(lleft));
  logicalright logicalright_1 (.In(In), .sh(sh), .Out(lright));
  arithright arithright_1 (.In(In), .sh(sh), .Out(aright));
  rotateleft rotateleft_1 (.In(In), .sh(sh), .Out(rleft));
  rotateright rotateright_1 (.In(In), .sh(sh), .Out(rright));
  Multiplexer #(.select(3), .width(32), .disabled(0), .enable("false")) multiplexer_1 (
    .in0(lleft), .in1(lright), .in2(aright), .in3(rleft), .in4(rright), .out(Out), .sel(op));  // open: in5, in6, in7
  Pull_Resistor pull_resistor_1 (.node(Out));

  // Notes on the sheet:
  //   移位器：In 32位输入，sh 5位输入-移位的数目，op 3位 操作种类
  //   op对应的操作种类： 000:左移，001:逻辑右移，010:算术右移，011:循环左移，100: 循环右移
endmodule

module logicalleft (
  input  [31:0] In,
  input  [4:0] sh,
  output [31:0] Out
);

  wire [31:0] multiplexer_1_out, multiplexer_2_out, multiplexer_3_out;
  wire [31:16] multiplexer_4_out, multiplexer_4_out_2;

  Multiplexer #(.width(32), .disabled(0), .enable("false")) multiplexer_1 (
    .in0(In), .in1({In[30:0], 1'b0}), .out(multiplexer_1_out), .sel(sh[0]));
  Multiplexer #(.width(32), .disabled(0), .enable("false")) multiplexer_2 (
    .in0(multiplexer_1_out), .in1({multiplexer_1_out[29:0], 2'b00}), .out(multiplexer_2_out), .sel(sh[1]));
  Multiplexer #(.width(32), .disabled(0), .enable("false")) multiplexer_3 (
    .in0(multiplexer_2_out), .in1({multiplexer_2_out[27:0], 4'b0000}), .out(multiplexer_3_out), .sel(sh[2]));
  Multiplexer #(.width(32), .disabled(0), .enable("false")) multiplexer_4 (
    .in0(multiplexer_3_out), .in1({multiplexer_3_out[23:0], {8{1'b0}}}),
    .out({multiplexer_4_out_2, multiplexer_4_out}), .sel(sh[3]));
  Multiplexer #(.width(32), .disabled(0), .enable("false")) multiplexer_5 (
    .in0({multiplexer_4_out_2, multiplexer_4_out}), .in1({multiplexer_4_out, {16{1'b0}}}), .out(Out),
    .sel(sh[4]));
endmodule

module logicalright (
  input  [31:0] In,
  input  [4:0] sh,
  output [31:0] Out
);

  wire [31:0] multiplexer_1_out, multiplexer_2_out, multiplexer_3_out, multiplexer_4_out;

  Multiplexer #(.width(32), .disabled(0), .enable("false")) multiplexer_1 (
    .in0(In), .in1({1'b0, In[31:1]}), .out(multiplexer_1_out), .sel(sh[0]));
  Multiplexer #(.width(32), .disabled(0), .enable("false")) multiplexer_2 (
    .in0(multiplexer_1_out), .in1({2'b00, multiplexer_1_out[31:2]}), .out(multiplexer_2_out), .sel(sh[1]));
  Multiplexer #(.width(32), .disabled(0), .enable("false")) multiplexer_3 (
    .in0(multiplexer_2_out), .in1({4'b0000, multiplexer_2_out[31:4]}), .out(multiplexer_3_out), .sel(sh[2]));
  Multiplexer #(.width(32), .disabled(0), .enable("false")) multiplexer_4 (
    .in0(multiplexer_3_out), .in1({{8{1'b0}}, multiplexer_3_out[31:8]}), .out(multiplexer_4_out), .sel(sh[3]));
  Multiplexer #(.width(32), .disabled(0), .enable("false")) multiplexer_5 (
    .in0(multiplexer_4_out), .in1({{16{1'b0}}, multiplexer_4_out[31:16]}), .out(Out), .sel(sh[4]));
endmodule

module arithright (
  input  [31:0] In,
  input  [4:0] sh,
  output [31:0] Out
);

  wire [31:0] multiplexer_1_out, multiplexer_2_out, multiplexer_3_out, multiplexer_4_out;

  Multiplexer #(.width(32), .disabled(0), .enable("false")) multiplexer_1 (
    .in0(In), .in1({{2{In[31]}}, In[30:1]}), .out(multiplexer_1_out), .sel(sh[0]));
  Multiplexer #(.width(32), .disabled(0), .enable("false")) multiplexer_2 (
    .in0(multiplexer_1_out), .in1({{2{In[31]}}, multiplexer_1_out[31:2]}), .out(multiplexer_2_out),
    .sel(sh[1]));
  Multiplexer #(.width(32), .disabled(0), .enable("false")) multiplexer_3 (
    .in0(multiplexer_2_out), .in1({{4{In[31]}}, multiplexer_2_out[31:4]}), .out(multiplexer_3_out),
    .sel(sh[2]));
  Multiplexer #(.width(32), .disabled(0), .enable("false")) multiplexer_4 (
    .in0(multiplexer_3_out), .in1({{8{In[31]}}, multiplexer_3_out[31:8]}), .out(multiplexer_4_out),
    .sel(sh[3]));
  Multiplexer #(.width(32), .disabled(0), .enable("false")) multiplexer_5 (
    .in0(multiplexer_4_out), .in1({{16{In[31]}}, multiplexer_4_out[31:16]}), .out(Out), .sel(sh[4]));

  // Other names for the same wires on the sheet: sign = In[31]
endmodule

module rotateleft (
  input  [31:0] In,
  input  [4:0] sh,
  output [31:0] Out
);

  wire [1:0] L1;
  wire [3:0] L2;
  wire [7:0] L3;
  wire [15:0] L4, multiplexer_4_out;
  wire [23:0] multiplexer_3_out;
  wire [27:0] multiplexer_2_out;
  wire [29:0] multiplexer_1_out;

  Multiplexer #(.width(32), .disabled(0), .enable("false")) multiplexer_1 (
    .in0(In), .in1({In[30:0], In[31]}), .out({L1, multiplexer_1_out}), .sel(sh[0]));
  Multiplexer #(.width(32), .disabled(0), .enable("false")) multiplexer_2 (
    .in0({L1, multiplexer_1_out}), .in1({multiplexer_1_out, L1}), .out({L2, multiplexer_2_out}), .sel(sh[1]));
  Multiplexer #(.width(32), .disabled(0), .enable("false")) multiplexer_3 (
    .in0({L2, multiplexer_2_out}), .in1({multiplexer_2_out, L2}), .out({L3, multiplexer_3_out}), .sel(sh[2]));
  Multiplexer #(.width(32), .disabled(0), .enable("false")) multiplexer_4 (
    .in0({L3, multiplexer_3_out}), .in1({multiplexer_3_out, L3}), .out({L4, multiplexer_4_out}), .sel(sh[3]));
  Multiplexer #(.width(32), .disabled(0), .enable("false")) multiplexer_5 (
    .in0({L4, multiplexer_4_out}), .in1({multiplexer_4_out, L4}), .out(Out), .sel(sh[4]));

  // Other names for the same wires on the sheet: L0 = In[31]
endmodule

module rotateright (
  input  [31:0] In,
  input  [4:0] sh,
  output [31:0] Out
);

  wire [1:0] L1;
  wire [3:0] L2;
  wire [7:0] L3;
  wire [15:0] L4;
  wire [31:2] multiplexer_1_out;
  wire [31:4] multiplexer_2_out;
  wire [31:8] multiplexer_3_out;
  wire [31:16] multiplexer_4_out;

  Multiplexer #(.width(32), .disabled(0), .enable("false")) multiplexer_1 (
    .in0(In), .in1({In[0], In[31:1]}), .out({multiplexer_1_out, L1}), .sel(sh[0]));
  Multiplexer #(.width(32), .disabled(0), .enable("false")) multiplexer_2 (
    .in0({multiplexer_1_out, L1}), .in1({L1, multiplexer_1_out}), .out({multiplexer_2_out, L2}), .sel(sh[1]));
  Multiplexer #(.width(32), .disabled(0), .enable("false")) multiplexer_3 (
    .in0({multiplexer_2_out, L2}), .in1({L2, multiplexer_2_out}), .out({multiplexer_3_out, L3}), .sel(sh[2]));
  Multiplexer #(.width(32), .disabled(0), .enable("false")) multiplexer_4 (
    .in0({multiplexer_3_out, L3}), .in1({L3, multiplexer_3_out}), .out({multiplexer_4_out, L4}), .sel(sh[3]));
  Multiplexer #(.width(32), .disabled(0), .enable("false")) multiplexer_5 (
    .in0({multiplexer_4_out, L4}), .in1({L4, multiplexer_4_out}), .out(Out), .sel(sh[4]));

  // Other names for the same wires on the sheet: L0 = In[0]
endmodule
