// Logisim project state.circ as structural Verilog: 7 circuits, main circuit tests
module PC (
  input  clk,
  input  rst,
  input  [31:0] nextPC,
  output [31:0] PC
);

  wire init;
  wire [31:0] PC_q;

  Counter #(.width(1), .max('h1), .ongoal("stay")) initcnt (
    .carry(init), .clk(clk), .clr(rst));  // open: load, D, count, Q
  Register #(.width(32)) u_PC (.D(nextPC), .Q(PC_q), .clk(clk), .clr(rst));  // open: en
  Multiplexer #(.width(32), .disabled(0), .enable("false")) multiplexer_1 (
    .in0({32{1'b0}}), .in1(PC_q), .out(PC), .sel(init));

  // Notes on the sheet:
  //   Program Counter: 指令计数器
  //   如果PC的初始值是0x00003000则修改MUX处的常量
endmodule

module GRF (
  input  clk,
  input  reset,
  input  WE,
  input  [4:0] A1,
  input  [4:0] A2,
  input  [4:0] A3,
  input  [31:0] WD,
  output [31:0] RD1,
  output [31:0] RD2
);

  wire E1, E2, E3, E4, E5, E6, E7, E8, E9, E10, E11, E12, E13, E14, E15, E16, E17, E18, E19, E20, E21, E22,
       E23, E24, E25, E26, E27, E28, E29, E30, E31;
  wire [31:0] D1, D2, D3, D4, D5, D6, D7, D8, D9, D10, D11, D12, D13, D14, D15, D16, D17, D18, D19, D20, D21,
       D22, D23, D24, D25, D26, D27, D28, D29, D30, D31, Q0, Q1, Q2, Q3, Q4, Q5, Q6, Q7, Q8, Q9, Q10, Q11,
       Q12, Q13, Q14, Q15, Q16, Q17, Q18, Q19, Q20, Q21, Q22, Q23, Q24, Q25, Q26, Q27, Q28, Q29, Q30, Q31;

  Demultiplexer #(.select(5), .disabled(0), .enable("false")) demultiplexer_1 (
    .out1(E1), .out2(E2), .out3(E3), .out4(E4), .out5(E5), .out6(E6), .out7(E7), .out8(E8), .out9(E9),
    .out10(E10), .out11(E11), .out12(E12), .out13(E13), .out14(E14), .out15(E15), .out16(E16), .out17(E17),
    .out18(E18), .out19(E19), .out20(E20), .out21(E21), .out22(E22), .out23(E23), .out24(E24), .out25(E25),
    .out26(E26), .out27(E27), .out28(E28), .out29(E29), .out30(E30), .out31(E31), .in(WE), .sel(A3));  // open: out0
  Register #(.width(32)) reg0 (.en(1'b0), .Q(Q0), .clk(clk), .clr(reset));  // open: D
  Register #(.width(32)) reg8 (.D(D8), .en(E8), .Q(Q8), .clk(clk), .clr(reset));
  Register #(.width(32)) reg16 (.D(D16), .en(E16), .Q(Q16), .clk(clk), .clr(reset));
  Register #(.width(32)) reg24 (.D(D24), .en(E24), .Q(Q24), .clk(clk), .clr(reset));
  Register #(.width(32)) reg1 (.D(D1), .en(E1), .Q(Q1), .clk(clk), .clr(reset));
  Register #(.width(32)) reg9 (.D(D9), .en(E9), .Q(Q9), .clk(clk), .clr(reset));
  Register #(.width(32)) reg17 (.D(D17), .en(E17), .Q(Q17), .clk(clk), .clr(reset));
  Register #(.width(32)) reg25 (.D(D25), .en(E25), .Q(Q25), .clk(clk), .clr(reset));
  Demultiplexer #(.select(5), .width(32), .disabled(0), .enable("false")) demultiplexer_2 (
    .out1(D1), .out2(D2), .out3(D3), .out4(D4), .out5(D5), .out6(D6), .out7(D7), .out8(D8), .out9(D9),
    .out10(D10), .out11(D11), .out12(D12), .out13(D13), .out14(D14), .out15(D15), .out16(D16), .out17(D17),
    .out18(D18), .out19(D19), .out20(D20), .out21(D21), .out22(D22), .out23(D23), .out24(D24), .out25(D25),
    .out26(D26), .out27(D27), .out28(D28), .out29(D29), .out30(D30), .out31(D31), .in(WD), .sel(A3));  // open: out0
  Register #(.width(32)) reg2 (.D(D2), .en(E2), .Q(Q2), .clk(clk), .clr(reset));
  Register #(.width(32)) reg10 (.D(D10), .en(E10), .Q(Q10), .clk(clk), .clr(reset));
  Register #(.width(32)) reg18 (.D(D18), .en(E18), .Q(Q18), .clk(clk), .clr(reset));
  Register #(.width(32)) reg26 (.D(D26), .en(E26), .Q(Q26), .clk(clk), .clr(reset));
  Register #(.width(32)) reg3 (.D(D3), .en(E3), .Q(Q3), .clk(clk), .clr(reset));
  Register #(.width(32)) reg11 (.D(D11), .en(E11), .Q(Q11), .clk(clk), .clr(reset));
  Register #(.width(32)) reg19 (.D(D19), .en(E19), .Q(Q19), .clk(clk), .clr(reset));
  Register #(.width(32)) reg27 (.D(D27), .en(E27), .Q(Q27), .clk(clk), .clr(reset));
  Register #(.width(32)) reg4 (.D(D4), .en(E4), .Q(Q4), .clk(clk), .clr(reset));
  Register #(.width(32)) reg12 (.D(D12), .en(E12), .Q(Q12), .clk(clk), .clr(reset));
  Register #(.width(32)) reg20 (.D(D20), .en(E20), .Q(Q20), .clk(clk), .clr(reset));
  Register #(.width(32)) reg28 (.D(D28), .en(E28), .Q(Q28), .clk(clk), .clr(reset));
  Multiplexer #(.select(5), .width(32), .disabled(0), .enable("false")) multiplexer_1 (
    .in0(Q0), .in1(Q1), .in2(Q2), .in3(Q3), .in4(Q4), .in5(Q5), .in6(Q6), .in7(Q7), .in8(Q8), .in9(Q9),
    .in10(Q10), .in11(Q11), .in12(Q12), .in13(Q13), .in14(Q14), .in15(Q15), .in16(Q16), .in17(Q17),
    .in18(Q18), .in19(Q19), .in20(Q20), .in21(Q21), .in22(Q22), .in23(Q23), .in24(Q24), .in25(Q25),
    .in26(Q26), .in27(Q27), .in28(Q28), .in29(Q29), .in30(Q30), .in31(Q31), .out(RD1), .sel(A1));
  Register #(.width(32)) reg5 (.D(D5), .en(E5), .Q(Q5), .clk(clk), .clr(reset));
  Register #(.width(32)) reg13 (.D(D13), .en(E13), .Q(Q13), .clk(clk), .clr(reset));
  Register #(.width(32)) reg21 (.D(D21), .en(E21), .Q(Q21), .clk(clk), .clr(reset));
  Register #(.width(32)) reg29 (.D(D29), .en(E29), .Q(Q29), .clk(clk), .clr(reset));
  Register #(.width(32)) reg6 (.D(D6), .en(E6), .Q(Q6), .clk(clk), .clr(reset));
  Register #(.width(32)) reg14 (.D(D14), .en(E14), .Q(Q14), .clk(clk), .clr(reset));
  Register #(.width(32)) reg22 (.D(D22), .en(E22), .Q(Q22), .clk(clk), .clr(reset));
  Register #(.width(32)) reg30 (.D(D30), .en(E30), .Q(Q30), .clk(clk), .clr(reset));
  Multiplexer #(.select(5), .width(32), .disabled(0), .enable("false")) multiplexer_2 (
    .in0(Q0), .in1(Q1), .in2(Q2), .in3(Q3), .in4(Q4), .in5(Q5), .in6(Q6), .in7(Q7), .in8(Q8), .in9(Q9),
    .in10(Q10), .in11(Q11), .in12(Q12), .in13(Q13), .in14(Q14), .in15(Q15), .in16(Q16), .in17(Q17),
    .in18(Q18), .in19(Q19), .in20(Q20), .in21(Q21), .in22(Q22), .in23(Q23), .in24(Q24), .in25(Q25),
    .in26(Q26), .in27(Q27), .in28(Q28), .in29(Q29), .in30(Q30), .in31(Q31), .out(RD2), .sel(A2));
  Register #(.width(32)) reg7 (.D(D7), .en(E7), .Q(Q7), .clk(clk), .clr(reset));
  Register #(.width(32)) reg15 (.D(D15), .en(E15), .Q(Q15), .clk(clk), .clr(reset));
  Register #(.width(32)) reg23 (.D(D23), .en(E23), .Q(Q23), .clk(clk), .clr(reset));
  Register #(.width(32)) reg31 (.D(D31), .en(E31), .Q(Q31), .clk(clk), .clr(reset));
endmodule

module IM (
  input  [31:0] A,
  output [31:0] RD
);

  wire [23:0] im_addr_1_addr24;

  // Probe on A
  im_addr im_addr_1 (.Addr32(A), .Addr24(im_addr_1_addr24));
  ROM #(.addrWidth(24), .dataWidth(32)) rom_1 (.addr(im_addr_1_addr24), .data(RD), .sel(1'b1));
  // Probe on RD

  // Notes on the sheet:
  //   Instruction Memory 指令存储器
  //   im_addr模块将32位的PC转化成24位的ROM地址
  //   若PC有其他要求(例如从0x00003000开始，则修改此模块)
endmodule

module DM (
  input  clk,
  input  rst,
  input  WE,
  input  [31:0] A,
  input  [31:0] WD,
  output [31:0] RD
);

  wire [23:0] dm_addr_1_addr24;

  // Probe on A
  // Probe on WD
  dm_addr dm_addr_1 (.Addr32(A), .Addr24(dm_addr_1_addr24));
  RAM #(.addrWidth(24), .dataWidth(32), .bus("separate")) ram_1 (
    .addr(dm_addr_1_addr24), .din(WD), .data(RD), .str(WE), .sel(1'b1), .clk(clk), .ld(1'b1), .clr(rst));

  // Notes on the sheet:
  //   Data Memory 数据存储器
endmodule

module im_addr (
  input  [31:0] Addr32,
  output [23:0] Addr24
);

  wire [31:0] shifter_1_out;

  Shifter #(.width(32), .shift("lr")) shifter_1 (.in(Addr32), .\dist (5'b00010), .out(shifter_1_out));
  Bit_Extender #(.in_width(32), .out_width(24)) bit_extender_1 (.in(shifter_1_out), .out(Addr24));

  // Notes on the sheet:
  //   im_addr: 将32位的地址转化为24位的适合ROM的地址
  //   注：若PC地址从0x00003000开始，则修改该模块！！！！
endmodule

module dm_addr (
  input  [31:0] Addr32,
  output [23:0] Addr24
);

  wire [31:0] shifter_1_out;

  Shifter #(.width(32), .shift("lr")) shifter_1 (.in(Addr32), .\dist (5'b00010), .out(shifter_1_out));
  Bit_Extender #(.in_width(32), .out_width(24)) bit_extender_1 (.in(shifter_1_out), .out(Addr24));

  // Notes on the sheet:
  //   dm_addr: 将DM的32位输入地址转化成24位的RAM地址
endmodule

module tests (
  input  [31:0] in_1,
  input  [31:0] in_2,
  input  in_3,
  input  [31:0] in_4,
  input  in_5,
  input  [31:0] in_6,
  input  [4:0] in_7,
  input  in_8,
  input  [4:0] in_9,
  input  [4:0] in_10,
  input  in_11,
  input  [31:0] in_12
);

  wire clock_1_out, clock_2_out, clock_3_out;
  wire [31:0] dm_1_rd, grf_1_rd1, grf_1_rd2, im_1_rd, pc_1_pc;

  Clock clock_1 (.out(clock_1_out));
  // Probe on in_1
  // Probe on in_4
  Clock clock_2 (.out(clock_2_out));
  // Probe on in_12
  // Probe on pc_1_pc
  PC pc_1 (.nextPC(in_1), .PC(pc_1_pc), .clk(clock_1_out));  // open: rst
  IM im_1 (.A(in_4), .RD(im_1_rd));
  // Probe on im_1_rd
  // Probe on grf_1_rd1
  GRF grf_1 (
    .A1(in_7), .A2(in_9), .A3(in_10), .WD(in_12), .RD1(grf_1_rd1), .RD2(grf_1_rd2), .clk(clock_2_out),
    .reset(in_11), .WE(in_8));
  // Probe on grf_1_rd2
  // Probe on in_2
  // Probe on in_6
  // Probe on dm_1_rd
  DM dm_1 (.A(in_2), .WD(in_6), .RD(dm_1_rd), .clk(clock_3_out), .rst(in_5), .WE(in_3));
  Clock clock_3 (.out(clock_3_out));
endmodule
