// Logisim project tb.circ as structural Verilog: 4 circuits, main circuit tester
module tester (
  output [31:0] Instr,
  output RegWrite,
  output [4:0] RegAddr,
  output [31:0] RegData,
  output MemWrite,
  output [4:0] MemAddr,
  output [31:0] MemData,
  output halt
);

  wire clock_1_out, main_1_p1;
  wire [3:0] hex2dec_1_hi, hex2dec_1_lo, mask32_1_out_2, mask32_1_out_3, mask32_1_out_4, mask32_2_out_2,
       mask32_2_out_3, mask32_2_out_4, shifter_1_out, shifter_1_out_2;
  wire [4:0] mask5_1_out, mask5_2_out;
  wire [7:0] bit_extender_1_out, counter_1_q;
  wire [19:0] mask32_1_out, mask32_2_out;

  Clock clock_1 (.out(clock_1_out));
  // CPU_main main_1: pin names not known; wires that end beside it: main_1_p1, Instr, RegWrite, RegAddr, RegData, MemWrite, MemAddr, MemData
  Comparator comparator_1 (.a(8'h1), .b(counter_1_q), .gt(main_1_p1));  // open: eq, lt
  Counter #(.max('h1f), .ongoal("stay")) counter_1 (
    .Q(counter_1_q), .carry(halt), .clk(clock_1_out));  // open: load, D, count, clr
  mask5 mask5_1 (.in(MemAddr), .en(MemWrite), .out(mask5_1_out));
  mask5 mask5_2 (.in(RegAddr), .en(RegWrite), .out(mask5_2_out));
  assign bit_extender_1_out = {{3{1'b0}}, mask5_1_out};  // Bit_Extender bit_extender_1
  Hex_Digit_Display hex_digit_display_1 (.value(hex2dec_1_hi));  // open: dp
  Hex_Digit_Display hex_digit_display_2 (.value(hex2dec_1_lo));  // open: dp
  hex2dec hex2dec_1 (.hex5(mask5_2_out), .hi(hex2dec_1_hi), .lo(hex2dec_1_lo));
  Hex_Digit_Display hex_digit_display_3 (.value(shifter_1_out_2));  // open: dp
  Hex_Digit_Display hex_digit_display_4 (.value(shifter_1_out));  // open: dp
  Shifter shifter_1 (.in(bit_extender_1_out), .\dist (3'b010), .out({shifter_1_out_2, shifter_1_out}));
  Hex_Digit_Display hex_digit_display_5 (.value(Instr[27:24]));  // open: dp
  Hex_Digit_Display hex_digit_display_6 (.value(Instr[31:28]));  // open: dp
  Hex_Digit_Display hex_digit_display_7 (.value(mask32_1_out_3));  // open: dp
  Hex_Digit_Display hex_digit_display_8 (.value(mask32_1_out_4));  // open: dp
  Hex_Digit_Display hex_digit_display_9 (.value(mask32_2_out_3));  // open: dp
  Hex_Digit_Display hex_digit_display_10 (.value(mask32_2_out_4));  // open: dp
  LED u_RegWrite (.in(RegWrite));
  Hex_Digit_Display hex_digit_display_11 (.value(Instr[19:16]));  // open: dp
  Hex_Digit_Display hex_digit_display_12 (.value(Instr[23:20]));  // open: dp
  Hex_Digit_Display hex_digit_display_13 (.value(mask32_1_out_2));  // open: dp
  Hex_Digit_Display hex_digit_display_14 (.value(mask32_1_out[19:16]));  // open: dp
  mask32 mask32_1 (.in(RegData), .en(RegWrite), .out({mask32_1_out_4, mask32_1_out_3, mask32_1_out_2, mask32_1_out}));
  Hex_Digit_Display hex_digit_display_15 (.value(mask32_2_out_2));  // open: dp
  Hex_Digit_Display hex_digit_display_16 (.value(mask32_2_out[19:16]));  // open: dp
  mask32 mask32_2 (.in(MemData), .en(MemWrite), .out({mask32_2_out_4, mask32_2_out_3, mask32_2_out_2, mask32_2_out}));
  LED u_MemWrite (.in(MemWrite));
  Hex_Digit_Display hex_digit_display_17 (.value(Instr[11:8]));  // open: dp
  Hex_Digit_Display hex_digit_display_18 (.value(Instr[15:12]));  // open: dp
  Hex_Digit_Display hex_digit_display_19 (.value(mask32_1_out[11:8]));  // open: dp
  Hex_Digit_Display hex_digit_display_20 (.value(mask32_1_out[15:12]));  // open: dp
  Hex_Digit_Display hex_digit_display_21 (.value(mask32_2_out[15:12]));  // open: dp
  Hex_Digit_Display hex_digit_display_22 (.value(mask32_2_out[11:8]));  // open: dp
  Hex_Digit_Display hex_digit_display_23 (.value(Instr[3:0]));  // open: dp
  Hex_Digit_Display hex_digit_display_24 (.value(Instr[7:4]));  // open: dp
  Hex_Digit_Display hex_digit_display_25 (.value(mask32_1_out[7:4]));  // open: dp
  Hex_Digit_Display hex_digit_display_26 (.value(mask32_1_out[3:0]));  // open: dp
  Hex_Digit_Display hex_digit_display_27 (.value(mask32_2_out[7:4]));  // open: dp
  Hex_Digit_Display hex_digit_display_28 (.value(mask32_2_out[3:0]));  // open: dp

  // Notes on the sheet:
  //   写寄存器
  //   $
  //   写内存
  //   *
  //   <=
  //   <=
  //   当前指令
endmodule

module hex2dec (
  input  [4:0] hex5,
  output [3:0] hi,
  output [3:0] lo
);

  wire [4:0] divider_1_out, divider_1_rem;

  // Probe on hex5
  Divider #(.width(5)) divider_1 (.a(hex5), .b(5'b01010), .out(divider_1_out), .rem(divider_1_rem));  // open: upper
  Bit_Extender #(.in_width(5), .out_width(4)) bit_extender_1 (.in(divider_1_out), .out(hi));
  Bit_Extender #(.in_width(5), .out_width(4)) bit_extender_2 (.in(divider_1_rem), .out(lo));
  // Probe on hi
  // Probe on lo

  // Notes on the sheet:
  //   十六进制转十进制电路
  //   将5bit-十六进制转化成2位十进制
endmodule

module mask5 (
  input  [4:0] in,
  input  en,
  output [4:0] out
);

  Multiplexer #(.width(5), .enable("false")) multiplexer_1 (.in1(in), .out(out), .sel(en));  // open: in0
endmodule

module mask32 (
  input  [31:0] in,
  input  en,
  output [31:0] out
);

  Multiplexer #(.width(32), .enable("false")) multiplexer_1 (.in1(in), .out(out), .sel(en));  // open: in0
endmodule
